// Logisim project mar.circ as structural Verilog
module main (
  input  [11:0] in_1,
  input  [15:0] in_2
);

  wire button_1_out, button_2_out, button_3_out, button_4_out, button_5_out, button_6_out, button_7_out,
       button_8_out, button_9_out, button_10_out, button_11_out, button_12_out, button_13_out, button_14_out,
       button_15_out, button_16_out, controlunit_1_cr, controlunit_1_incpc, controlunit_1_lalt,
       controlunit_1_stop, demultiplexer_1_out1, demultiplexer_1_out2, demultiplexer_1_out3,
       demultiplexer_1_out4, demultiplexer_1_out5, demultiplexer_1_out6, demultiplexer_1_out7, enclock_1_cl,
       or_1_out, START_out;
  wire [1:0] controlunit_1_a0, controlunit_1_mw;
  wire [3:0] multiplexer_1_out, multiplexer_1_out_2, multiplexer_1_out_3, multiplexer_1_out_4, outReg_q,
       outReg_q_2, outReg_q_3, outReg_q_4;
  wire [5:0] controlunit_1_p0;
  wire [7:0] cyclecount_1_t0;
  wire [11:0] MAR_q;
  wire [15:0] AC_q, alu_1_aco, incpc_1_addout, InReg_q, IR_q, MBR_q, merger_1_outp, PC_q, pcmerger_1_outp,
       ram_1_dout, testkeyboard_1_keyout, toggle_1_o1, toggle_1_o2, toggle_2_o1, toggle_2_o2;

  Demultiplexer #(.select(3)) demultiplexer_1 (
    .out1(demultiplexer_1_out1), .out2(demultiplexer_1_out2), .out3(demultiplexer_1_out3),
    .out4(demultiplexer_1_out4), .out5(demultiplexer_1_out5), .out6(demultiplexer_1_out6),
    .out7(demultiplexer_1_out7), .in(1'b1), .sel(controlunit_1_p0[5:3]));  // open: out0
  RAM #(.addrWidth(12), .asyncread("true"), .dataWidth(16)) ram_1 (
    .addr(MAR_q), .we(controlunit_1_mw[0]), .oe(controlunit_1_mw[1]), .clk(enclock_1_cl),
    .din({multiplexer_1_out_4, multiplexer_1_out_3, multiplexer_1_out_2, multiplexer_1_out}),
    .dout(ram_1_dout));
  Merger merger_1 (
    .Busin({multiplexer_1_out_4, multiplexer_1_out_3, multiplexer_1_out_2, multiplexer_1_out}),
    .DataIn(alu_1_aco), .switch(controlunit_1_lalt), .outp(merger_1_outp));
  incpc incpc_1 (
    .Busin({multiplexer_1_out_4, multiplexer_1_out_3, multiplexer_1_out_2, multiplexer_1_out}),
    .EN(controlunit_1_incpc), .addout(incpc_1_addout));
  Register #(.width(12)) MAR (
    .D({multiplexer_1_out_3, multiplexer_1_out_2, multiplexer_1_out}), .en(demultiplexer_1_out1),
    .clk(enclock_1_cl), .Q(MAR_q));  // open: clr
  Register #(.width(16)) PC (
    .D(pcmerger_1_outp), .en(demultiplexer_1_out2), .clk(enclock_1_cl), .Q(PC_q));  // open: clr
  pcmerger pcmerger_1 (
    .BussIn({multiplexer_1_out_4, multiplexer_1_out_3, multiplexer_1_out_2, multiplexer_1_out}),
    .DataIn(incpc_1_addout), .switch(controlunit_1_incpc), .outp(pcmerger_1_outp));
  Register #(.width(16)) MBR (
    .D({multiplexer_1_out_4, multiplexer_1_out_3, multiplexer_1_out_2, multiplexer_1_out}),
    .en(demultiplexer_1_out3), .clk(enclock_1_cl), .Q(MBR_q));  // open: clr
  Register #(.width(16)) AC (.D(merger_1_outp), .en(demultiplexer_1_out4), .clk(enclock_1_cl), .Q(AC_q));  // open: clr
  Register #(.width(16)) InReg (.D(in_2), .en(1'b1), .clk(enclock_1_cl), .Q(InReg_q));  // open: clr
  Register #(.width(16)) outReg (
    .D({multiplexer_1_out_4, multiplexer_1_out_3, multiplexer_1_out_2, multiplexer_1_out}),
    .en(demultiplexer_1_out6), .clk(enclock_1_cl), .Q({outReg_q_4, outReg_q_3, outReg_q_2, outReg_q}));  // open: clr
  Register #(.width(16)) IR (
    .D({multiplexer_1_out_4, multiplexer_1_out_3, multiplexer_1_out_2, multiplexer_1_out}),
    .en(demultiplexer_1_out7), .clk(enclock_1_cl), .Q(IR_q));  // open: clr
  toggle toggle_1 (.i(MBR_q), .T(controlunit_1_lalt), .o1(toggle_1_o1), .o2(toggle_1_o2));
  toggle toggle_2 (.i(AC_q), .T(controlunit_1_lalt), .o1(toggle_2_o1), .o2(toggle_2_o2));
  ControlUnit controlunit_1 (
    .Instruction(IR_q), .RingCounter(cyclecount_1_t0), .AC(AC_q), .En(1'b1), .P1(controlunit_1_p0[1]),
    .P2(controlunit_1_p0[2]), .P3(controlunit_1_p0[3]), .P4(controlunit_1_p0[4]), .P5(controlunit_1_p0[5]),
    .A0(controlunit_1_a0[0]), .A1(controlunit_1_a0[1]), .Cr(controlunit_1_cr), .Mr(controlunit_1_mw[1]),
    .Mw(controlunit_1_mw[0]), .Lalt(controlunit_1_lalt), .IncPC(controlunit_1_incpc),
    .STOP(controlunit_1_stop), .P0(controlunit_1_p0[0]));
  Multiplexer #(.select(3), .width(16)) multiplexer_1 (
    .in0(ram_1_dout), .in1({4'b0000, MAR_q}), .in2(PC_q), .in3(toggle_1_o1), .in4(toggle_2_o1),
    .in5(InReg_q), .in7(IR_q),
    .out({multiplexer_1_out_4, multiplexer_1_out_3, multiplexer_1_out_2, multiplexer_1_out}),
    .sel(controlunit_1_p0[2:0]));  // open: in6
  ALU alu_1 (
    .A0(controlunit_1_a0[0]), .A1(controlunit_1_a0[1]), .ACi(toggle_2_o2), .MBR(toggle_1_o2), .ACo(alu_1_aco));  // open: Zero, Carry, Negative
  Hex_Digit_Display hex_digit_display_1 (.value(multiplexer_1_out_4));  // open: dp
  Hex_Digit_Display hex_digit_display_2 (.value(multiplexer_1_out_3));  // open: dp
  Hex_Digit_Display hex_digit_display_3 (.value(outReg_q_4));  // open: dp
  Hex_Digit_Display hex_digit_display_4 (.value(outReg_q_3));  // open: dp
  or or_1 (or_1_out, controlunit_1_stop, START_out);
  enClock enclock_1 (.toggle(or_1_out), .Cl(enclock_1_cl));
  Hex_Digit_Display hex_digit_display_5 (.value(multiplexer_1_out_2));  // open: dp
  Hex_Digit_Display hex_digit_display_6 (.value(multiplexer_1_out));  // open: dp
  Hex_Digit_Display hex_digit_display_7 (.value(outReg_q_2));  // open: dp
  Hex_Digit_Display hex_digit_display_8 (.value(outReg_q));  // open: dp
  Button START (.out(START_out));
  cyclecount cyclecount_1 (
    .Clock(enclock_1_cl), .Cr(controlunit_1_cr), .T0(cyclecount_1_t0[0]), .T1(cyclecount_1_t0[1]),
    .T2(cyclecount_1_t0[2]), .T3(cyclecount_1_t0[3]), .T4(cyclecount_1_t0[4]), .T5(cyclecount_1_t0[5]),
    .T6(cyclecount_1_t0[6]), .T7(cyclecount_1_t0[7]));
  Button button_1 (.out(button_1_out));
  Button button_2 (.out(button_2_out));
  Button button_3 (.out(button_3_out));
  Button button_4 (.out(button_4_out));
  Button button_5 (.out(button_5_out));
  Button button_6 (.out(button_6_out));
  Button button_7 (.out(button_7_out));
  Button button_8 (.out(button_8_out));
  Button button_9 (.out(button_9_out));
  Button button_10 (.out(button_10_out));
  Button button_11 (.out(button_11_out));
  Button button_12 (.out(button_12_out));
  Button button_13 (.out(button_13_out));
  Button button_14 (.out(button_14_out));
  Button button_15 (.out(button_15_out));
  Button button_16 (.out(button_16_out));
  testkeyboard testkeyboard_1 (
    .b0(button_1_out), .b1(button_2_out), .b2(button_3_out), .b3(button_4_out), .b4(button_5_out),
    .b5(button_6_out), .b6(button_7_out), .b7(button_8_out), .b8(button_9_out), .b9(button_10_out),
    .bA(button_11_out), .bB(button_12_out), .bC(button_13_out), .bD(button_14_out), .bE(button_15_out),
    .bF(button_16_out), .Data(in_1), .keyout(testkeyboard_1_keyout));
  Hex_Digit_Display hex_digit_display_9 (.value(testkeyboard_1_keyout[15:12]));  // open: dp
  Hex_Digit_Display hex_digit_display_10 (.value(testkeyboard_1_keyout[11:8]));  // open: dp
  Hex_Digit_Display hex_digit_display_11 (.value(testkeyboard_1_keyout[7:4]));  // open: dp
  Hex_Digit_Display hex_digit_display_12 (.value(testkeyboard_1_keyout[3:0]));  // open: dp

  // Notes on the sheet:
  //   p5 p4 p3
  //   p2 p1 p0
  //   Data Bus
  //   Output
endmodule

module cyclecount (
  input  Clock,
  input  Cr,
  output T0,
  output T1,
  output T2,
  output T3,
  output T4,
  output T5,
  output T6,
  output T7
);

  nor nor_1 (T0, T7, T6, T5, T4, T3, T2, T1);
  D_Flip_Flop D0 (.D(T0), .clk(Clock), .Q(T1));  // open: Qn, preset, reset
  D_Flip_Flop D1 (.D(T1), .clk(Clock), .Q(T2), .reset(Cr));  // open: Qn, preset
  D_Flip_Flop D2 (.D(T2), .clk(Clock), .Q(T3), .reset(Cr));  // open: Qn, preset
  D_Flip_Flop D3 (.D(T3), .clk(Clock), .Q(T4), .reset(Cr));  // open: Qn, preset
  D_Flip_Flop D4 (.D(T4), .clk(Clock), .Q(T5), .reset(Cr));  // open: Qn, preset
  D_Flip_Flop D5 (.D(T5), .clk(Clock), .Q(T6), .reset(Cr));  // open: Qn, preset
  D_Flip_Flop D6 (.D(T6), .clk(Clock), .Q(T7), .reset(Cr));  // open: Qn, preset

  // Notes on the sheet:
  //   Cr
  //   clock
endmodule

module testkeyboard (
  input  [11:0] Data,
  input  b0,
  input  b1,
  input  b2,
  input  b3,
  input  b4,
  input  b5,
  input  b6,
  input  b7,
  input  b8,
  input  b9,
  input  bA,
  input  bB,
  input  bC,
  input  bD,
  input  bE,
  input  bF,
  output [15:0] keyout
);

  wire priority_encoder_1_gs;
  wire [3:0] priority_encoder_1_out;

  Priority_Encoder #(.select(4)) priority_encoder_1 (
    .in0(b0), .in1(b1), .in2(b2), .in3(b3), .in4(b4), .in5(b5), .in6(b6), .in7(b7), .in8(b8), .in9(b9),
    .in10(bA), .in11(bB), .in12(bC), .in13(bD), .in14(bE), .in15(bF), .out(priority_encoder_1_out),
    .gs(priority_encoder_1_gs));  // open: en_out, en_in
  Register #(.width(4)) register_1 (
    .D(priority_encoder_1_out), .en(priority_encoder_1_gs), .clk(priority_encoder_1_gs), .Q(keyout[15:12]));  // open: clr

  assign keyout[11:0] = Data;
endmodule

module ControlUnit (
  input  [15:0] AC,
  input  En,
  input  [7:0] RingCounter,
  input  [15:0] Instruction,
  output STOP,
  output P0,
  output P1,
  output P2,
  output P3,
  output P4,
  output P5,
  output A0,
  output A1,
  output Cr,
  output Mr,
  output Mw,
  output Lalt,
  output IncPC
);

  wire add_1_a0, add_1_a1, add_1_cr, add_1_incpc, add_1_lalt, add_1_mr, add_1_mw, add_1_p0, add_1_p1,
       add_1_p2, add_1_p3, add_1_p4, add_1_p5, addi_1_a0, addi_1_a1, addi_1_cr, addi_1_incpc, addi_1_lalt,
       addi_1_mr, addi_1_mw, addi_1_p0, addi_1_p1, addi_1_p2, addi_1_p3, addi_1_p4, addi_1_p5, clear_1_a0,
       clear_1_a1, clear_1_cr, clear_1_incpc, clear_1_lalt, clear_1_mr, clear_1_mw, clear_1_p0, clear_1_p1,
       clear_1_p2, clear_1_p3, clear_1_p4, clear_1_p5, decoder_1_out0, decoder_1_out1, decoder_1_out2,
       decoder_1_out3, decoder_1_out4, decoder_1_out5, decoder_1_out6, decoder_1_out7, decoder_1_out8,
       decoder_1_out9, decoder_1_out10, decoder_1_out11, decoder_1_out12, decoder_1_out13, decoder_1_out14,
       decoder_1_out15, halt_1_a0, halt_1_a1, halt_1_cr, halt_1_incpc, halt_1_lalt, halt_1_mr, halt_1_mw,
       halt_1_p0, halt_1_p1, halt_1_p2, halt_1_p3, halt_1_p4, halt_1_p5, jns_1_a0, jns_1_a1, jns_1_cr,
       jns_1_incpc, jns_1_lalt, jns_1_mr, jns_1_mw, jns_1_p0, jns_1_p1, jns_1_p2, jns_1_p3, jns_1_p4,
       jns_1_p5, jump_1_a0, jump_1_a1, jump_1_cr, jump_1_incpc, jump_1_lalt, jump_1_mr, jump_1_mw, jump_1_p0,
       jump_1_p1, jump_1_p2, jump_1_p3, jump_1_p4, jump_1_p5, jumpi_1_a0, jumpi_1_a1, jumpi_1_cr,
       jumpi_1_incpc, jumpi_1_lalt, jumpi_1_mr, jumpi_1_mw, jumpi_1_p0, jumpi_1_p1, jumpi_1_p2, jumpi_1_p3,
       jumpi_1_p4, jumpi_1_p5, load_1_a0, load_1_a1, load_1_cr, load_1_incpc, load_1_lalt, load_1_mr,
       load_1_mw, load_1_p0, load_1_p1, load_1_p2, load_1_p3, load_1_p4, load_1_p5, loadi_1_a0, loadi_1_a1,
       loadi_1_cr, loadi_1_incpc, loadi_1_lalt, loadi_1_mr, loadi_1_mw, loadi_1_p0, loadi_1_p1, loadi_1_p2,
       loadi_1_p3, loadi_1_p4, loadi_1_p5, orconnect_14_out_3, orconnect_15_out_3, orconnect_16_out_3,
       orconnect_17_out_3, orconnect_18_out_3, orconnect_19_out_3, orconnect_20_out_3, orconnect_21_out_3,
       orconnect_22_out_3, orconnect_23_out_3, orconnect_24_out_3, orconnect_25_out_3, orconnect_26_out_3,
       orconnect_27_out_3, orconnect_28_out_3, orconnect_29_out_3, orconnect_30_out_3, orconnect_31_out_3,
       orconnect_32_out_3, orconnect_33_out_3, orconnect_34_out_3, orconnect_35_out_3, orconnect_36_out_3,
       orconnect_37_out_3, orconnect_38_out_3, orconnect_39_out_3, orconnect_40_out_3, orconnect_41_out_3,
       orconnect_42_out_3, orconnect_43_out_3, orconnect_44_out_3, orconnect_45_out_3, orconnect_46_out_3,
       orconnect_47_out_3, orconnect_48_out_3, orconnect_49_out_3, orconnect_50_out_3, orconnect_51_out_3,
       orconnect_52_out_3, orconnect_53_out_3, orconnect_54_out_3, orconnect_55_out_3, orconnect_56_out_3,
       orconnect_57_out_3, orconnect_58_out_3, orconnect_59_out_3, orconnect_60_out_3, orconnect_61_out_3,
       orconnect_62_out_3, orconnect_63_out_3, orconnect_64_out_3, orconnect_65_out_3, orconnect_66_out_3,
       orconnect_67_out_3, orconnect_68_out_3, orconnect_69_out_3, orconnect_70_out_3, orconnect_71_out_3,
       orconnect_72_out_3, orconnect_73_out_3, orconnect_74_out_3, orconnect_75_out_3, orconnect_76_out_3,
       orconnect_77_out_3, orconnect_78_out_3, orconnect_79_out_3, orconnect_80_out_3, orconnect_81_out_3,
       orconnect_82_out_3, orconnect_83_out_3, orconnect_84_out_3, orconnect_85_out_3, orconnect_86_out_3,
       orconnect_87_out_3, orconnect_88_out_3, orconnect_89_out_3, orconnect_90_out_3, orconnect_91_out_3,
       orconnect_92_out_3, orconnect_93_out_3, orconnect_94_out_3, orconnect_95_out_3, orconnect_96_out_3,
       orconnect_97_out_3, orconnect_98_out_3, orconnect_99_out_3, orconnect_100_out_3, orconnect_101_out_3,
       orconnect_102_out_3, orconnect_103_out_3, orconnect_104_out_3, orconnect_105_out_3,
       orconnect_106_out_3, orconnect_107_out_3, orconnect_108_out_3, orconnect_109_out_3,
       orconnect_110_out_3, orconnect_111_out_3, orconnect_112_out_3, orconnect_113_out_3,
       orconnect_114_out_3, orconnect_115_out_3, orconnect_116_out_3, orconnect_117_out_3,
       orconnect_118_out_3, orconnect_119_out_3, orconnect_120_out_3, orconnect_121_out_3,
       orconnect_122_out_3, orconnect_123_out_3, orconnect_124_out_3, orconnect_125_out_3,
       orconnect_126_out_3, orconnect_127_out_3, orconnect_128_out_3, orconnect_129_out_3,
       orconnect_130_out_3, orconnect_131_out_3, orconnect_132_out_3, orconnect_133_out_3,
       orconnect_134_out_3, orconnect_135_out_3, orconnect_136_out_3, orconnect_137_out_3,
       orconnect_138_out_3, orconnect_139_out_3, orconnect_140_out_3, orconnect_141_out_3,
       orconnect_142_out_3, orconnect_143_out_3, orconnect_144_out_3, orconnect_145_out_3,
       orconnect_146_out_3, orconnect_147_out_3, orconnect_148_out_3, orconnect_149_out_3,
       orconnect_150_out_3, orconnect_151_out_3, orconnect_152_out_3, orconnect_153_out_3,
       orconnect_154_out_3, orconnect_155_out_3, orconnect_156_out_3, orconnect_157_out_3,
       orconnect_158_out_3, orconnect_159_out_3, orconnect_160_out_3, orconnect_161_out_3,
       orconnect_162_out_3, orconnect_163_out_3, orconnect_164_out_3, orconnect_165_out_3,
       orconnect_166_out_3, orconnect_167_out_3, orconnect_168_out_3, orconnect_169_out_3,
       orconnect_170_out_3, orconnect_171_out_3, orconnect_172_out_3, orconnect_173_out_3,
       orconnect_174_out_3, orconnect_175_out_3, orconnect_176_out_3, orconnect_177_out_3,
       orconnect_178_out_3, orconnect_179_out_3, orconnect_180_out_3, orconnect_181_out_3,
       orconnect_182_out_3, orconnect_183_out_3, orconnect_184_out_3, orconnect_185_out_3,
       orconnect_186_out_3, orconnect_187_out_3, orconnect_188_out_3, orconnect_189_out_3,
       orconnect_190_out_3, orconnect_191_out_3, orconnect_192_out_3, orconnect_193_out_3,
       orconnect_194_out_3, orconnect_195_out_3, outpt_1_a0, outpt_1_a1, outpt_1_cr, outpt_1_incpc,
       outpt_1_lalt, outpt_1_mr, outpt_1_mw, outpt_1_p0, outpt_1_p1, outpt_1_p2, outpt_1_p3, outpt_1_p4,
       outpt_1_p5, skipcon_1_a0, skipcon_1_a1, skipcon_1_cr, skipcon_1_incpc, skipcon_1_lalt, skipcon_1_mr,
       skipcon_1_mw, skipcon_1_p0, skipcon_1_p1, skipcon_1_p2, skipcon_1_p3, skipcon_1_p4, skipcon_1_p5,
       store_1_a0, store_1_a1, store_1_cr, store_1_incpc, store_1_lalt, store_1_mr, store_1_mw, store_1_p0,
       store_1_p1, store_1_p2, store_1_p3, store_1_p4, store_1_p5, storei_1_a0, storei_1_a1, storei_1_cr,
       storei_1_incpc, storei_1_lalt, storei_1_mr, storei_1_mw, storei_1_p0, storei_1_p1, storei_1_p2,
       storei_1_p3, storei_1_p4, storei_1_p5, subt_1_a0, subt_1_a1, subt_1_cr, subt_1_incpc, subt_1_lalt,
       subt_1_mr, subt_1_mw, subt_1_p0, subt_1_p1, subt_1_p2, subt_1_p3, subt_1_p4, subt_1_p5,
       teststartload_1_a0, teststartload_1_a1, teststartload_1_cr, teststartload_1_lalt, teststartload_1_mr,
       teststartload_1_mw, teststartload_1_p0, teststartload_1_p1, teststartload_1_p2, teststartload_1_p3,
       teststartload_1_p4, teststartload_1_p5, valin_1_a0, valin_1_a1, valin_1_cr, valin_1_incpc,
       valin_1_lalt, valin_1_mr, valin_1_mw, valin_1_p0, valin_1_p1, valin_1_p2, valin_1_p3, valin_1_p4,
       valin_1_p5;

  Decoder #(.select(4)) decoder_1 (
    .out0(decoder_1_out0), .out1(decoder_1_out1), .out2(decoder_1_out2), .out3(decoder_1_out3),
    .out4(decoder_1_out4), .out5(decoder_1_out5), .out6(decoder_1_out6), .out7(decoder_1_out7),
    .out8(decoder_1_out8), .out9(decoder_1_out9), .out10(decoder_1_out10), .out11(decoder_1_out11),
    .out12(decoder_1_out12), .out13(decoder_1_out13), .out14(decoder_1_out14), .out15(decoder_1_out15),
    .sel(Instruction[15:12]), .en(En));
  orconnect orconnect_1 (.in_2(orconnect_18_out_3), .in_1(jns_1_mr), .out_3(Mr));
  orconnect orconnect_2 (.in_2(orconnect_19_out_3), .in_1(jns_1_mw), .out_3(Mw));
  orconnect orconnect_3 (.in_2(orconnect_20_out_3), .in_1(jns_1_lalt), .out_3(Lalt));
  orconnect orconnect_4 (.in_2(orconnect_21_out_3), .in_1(jns_1_incpc), .out_3(IncPC));
  JnS jns_1 (
    .EN(decoder_1_out0), .RingCounter(RingCounter), .P0(jns_1_p0), .P1(jns_1_p1), .P2(jns_1_p2),
    .P3(jns_1_p3), .P4(jns_1_p4), .P5(jns_1_p5), .A0(jns_1_a0), .A1(jns_1_a1), .Cr(jns_1_cr), .Mr(jns_1_mr),
    .Mw(jns_1_mw), .Lalt(jns_1_lalt), .IncPC(jns_1_incpc));
  orconnect orconnect_5 (.in_2(orconnect_23_out_3), .in_1(jns_1_p1), .out_3(P1));
  orconnect orconnect_6 (.in_2(orconnect_24_out_3), .in_1(jns_1_p2), .out_3(P2));
  orconnect orconnect_7 (.in_2(orconnect_25_out_3), .in_1(jns_1_p3), .out_3(P3));
  orconnect orconnect_8 (.in_2(orconnect_26_out_3), .in_1(jns_1_p4), .out_3(P4));
  orconnect orconnect_9 (.in_2(orconnect_14_out_3), .in_1(jns_1_p5), .out_3(P5));
  orconnect orconnect_10 (.in_2(orconnect_15_out_3), .in_1(jns_1_a0), .out_3(A0));
  orconnect orconnect_11 (.in_2(orconnect_16_out_3), .in_1(jns_1_a1), .out_3(A1));
  orconnect orconnect_12 (.in_2(orconnect_17_out_3), .in_1(jns_1_cr), .out_3(Cr));
  orconnect orconnect_13 (.in_2(orconnect_22_out_3), .in_1(jns_1_p0), .out_3(P0));
  orconnect orconnect_14 (.in_2(orconnect_35_out_3), .in_1(load_1_p5), .out_3(orconnect_14_out_3));
  orconnect orconnect_15 (.in_2(orconnect_36_out_3), .in_1(load_1_a0), .out_3(orconnect_15_out_3));
  orconnect orconnect_16 (.in_2(orconnect_37_out_3), .in_1(load_1_a1), .out_3(orconnect_16_out_3));
  orconnect orconnect_17 (.in_2(orconnect_38_out_3), .in_1(load_1_cr), .out_3(orconnect_17_out_3));
  orconnect orconnect_18 (.in_2(orconnect_27_out_3), .in_1(load_1_mr), .out_3(orconnect_18_out_3));
  orconnect orconnect_19 (.in_2(orconnect_28_out_3), .in_1(load_1_mw), .out_3(orconnect_19_out_3));
  orconnect orconnect_20 (.in_2(orconnect_29_out_3), .in_1(load_1_lalt), .out_3(orconnect_20_out_3));
  orconnect orconnect_21 (.in_2(orconnect_30_out_3), .in_1(load_1_incpc), .out_3(orconnect_21_out_3));
  Load load_1 (
    .EN(decoder_1_out1), .RingCounter(RingCounter), .P0(load_1_p0), .P1(load_1_p1), .P2(load_1_p2),
    .P3(load_1_p3), .P4(load_1_p4), .P5(load_1_p5), .A0(load_1_a0), .A1(load_1_a1), .Cr(load_1_cr),
    .Mr(load_1_mr), .Mw(load_1_mw), .Lalt(load_1_lalt), .incpc(load_1_incpc));
  orconnect orconnect_22 (.in_2(orconnect_39_out_3), .in_1(load_1_p0), .out_3(orconnect_22_out_3));
  orconnect orconnect_23 (.in_2(orconnect_31_out_3), .in_1(load_1_p1), .out_3(orconnect_23_out_3));
  orconnect orconnect_24 (.in_2(orconnect_32_out_3), .in_1(load_1_p2), .out_3(orconnect_24_out_3));
  orconnect orconnect_25 (.in_2(orconnect_33_out_3), .in_1(load_1_p3), .out_3(orconnect_25_out_3));
  orconnect orconnect_26 (.in_2(orconnect_34_out_3), .in_1(load_1_p4), .out_3(orconnect_26_out_3));
  orconnect orconnect_27 (.in_2(orconnect_44_out_3), .in_1(store_1_mr), .out_3(orconnect_27_out_3));
  orconnect orconnect_28 (.in_2(orconnect_45_out_3), .in_1(store_1_mw), .out_3(orconnect_28_out_3));
  orconnect orconnect_29 (.in_2(orconnect_46_out_3), .in_1(store_1_lalt), .out_3(orconnect_29_out_3));
  orconnect orconnect_30 (.in_2(orconnect_47_out_3), .in_1(store_1_incpc), .out_3(orconnect_30_out_3));
  Store store_1 (
    .EN(decoder_1_out2), .RingCounter(RingCounter), .P0(store_1_p0), .P1(store_1_p1), .P2(store_1_p2),
    .P3(store_1_p3), .P4(store_1_p4), .P5(store_1_p5), .A0(store_1_a0), .A1(store_1_a1), .Cr(store_1_cr),
    .Mr(store_1_mr), .Mw(store_1_mw), .Lalt(store_1_lalt), .incpc(store_1_incpc));
  orconnect orconnect_31 (.in_2(orconnect_49_out_3), .in_1(store_1_p1), .out_3(orconnect_31_out_3));
  orconnect orconnect_32 (.in_2(orconnect_50_out_3), .in_1(store_1_p2), .out_3(orconnect_32_out_3));
  orconnect orconnect_33 (.in_2(orconnect_51_out_3), .in_1(store_1_p3), .out_3(orconnect_33_out_3));
  orconnect orconnect_34 (.in_2(orconnect_52_out_3), .in_1(store_1_p4), .out_3(orconnect_34_out_3));
  orconnect orconnect_35 (.in_2(orconnect_40_out_3), .in_1(store_1_p5), .out_3(orconnect_35_out_3));
  orconnect orconnect_36 (.in_2(orconnect_41_out_3), .in_1(store_1_a0), .out_3(orconnect_36_out_3));
  orconnect orconnect_37 (.in_2(orconnect_42_out_3), .in_1(store_1_a1), .out_3(orconnect_37_out_3));
  orconnect orconnect_38 (.in_2(orconnect_43_out_3), .in_1(store_1_cr), .out_3(orconnect_38_out_3));
  orconnect orconnect_39 (.in_2(orconnect_48_out_3), .in_1(store_1_p0), .out_3(orconnect_39_out_3));
  orconnect orconnect_40 (.in_2(orconnect_61_out_3), .in_1(add_1_p5), .out_3(orconnect_40_out_3));
  orconnect orconnect_41 (.in_2(orconnect_62_out_3), .in_1(add_1_a0), .out_3(orconnect_41_out_3));
  orconnect orconnect_42 (.in_2(orconnect_63_out_3), .in_1(add_1_a1), .out_3(orconnect_42_out_3));
  orconnect orconnect_43 (.in_2(orconnect_64_out_3), .in_1(add_1_cr), .out_3(orconnect_43_out_3));
  orconnect orconnect_44 (.in_2(orconnect_53_out_3), .in_1(add_1_mr), .out_3(orconnect_44_out_3));
  orconnect orconnect_45 (.in_2(orconnect_54_out_3), .in_1(add_1_mw), .out_3(orconnect_45_out_3));
  orconnect orconnect_46 (.in_2(orconnect_55_out_3), .in_1(add_1_lalt), .out_3(orconnect_46_out_3));
  orconnect orconnect_47 (.in_2(orconnect_56_out_3), .in_1(add_1_incpc), .out_3(orconnect_47_out_3));
  Add add_1 (
    .En(decoder_1_out3), .RingCounter(RingCounter), .P0(add_1_p0), .P1(add_1_p1), .P2(add_1_p2),
    .P3(add_1_p3), .P4(add_1_p4), .P5(add_1_p5), .A0(add_1_a0), .A1(add_1_a1), .Cr(add_1_cr), .Mr(add_1_mr),
    .Mw(add_1_mw), .Lalt(add_1_lalt), .incpc(add_1_incpc));
  orconnect orconnect_48 (.in_2(orconnect_65_out_3), .in_1(add_1_p0), .out_3(orconnect_48_out_3));
  orconnect orconnect_49 (.in_2(orconnect_57_out_3), .in_1(add_1_p1), .out_3(orconnect_49_out_3));
  orconnect orconnect_50 (.in_2(orconnect_58_out_3), .in_1(add_1_p2), .out_3(orconnect_50_out_3));
  orconnect orconnect_51 (.in_2(orconnect_59_out_3), .in_1(add_1_p3), .out_3(orconnect_51_out_3));
  orconnect orconnect_52 (.in_2(orconnect_60_out_3), .in_1(add_1_p4), .out_3(orconnect_52_out_3));
  orconnect orconnect_53 (.in_2(orconnect_70_out_3), .in_1(subt_1_mr), .out_3(orconnect_53_out_3));
  orconnect orconnect_54 (.in_2(orconnect_71_out_3), .in_1(subt_1_mw), .out_3(orconnect_54_out_3));
  orconnect orconnect_55 (.in_2(orconnect_72_out_3), .in_1(subt_1_lalt), .out_3(orconnect_55_out_3));
  orconnect orconnect_56 (.in_2(orconnect_73_out_3), .in_1(subt_1_incpc), .out_3(orconnect_56_out_3));
  subt subt_1 (
    .En(decoder_1_out4), .RingCounter(RingCounter), .P0(subt_1_p0), .P1(subt_1_p1), .P2(subt_1_p2),
    .P3(subt_1_p3), .P4(subt_1_p4), .P5(subt_1_p5), .A0(subt_1_a0), .A1(subt_1_a1), .Cr(subt_1_cr),
    .Mr(subt_1_mr), .Mw(subt_1_mw), .Lalt(subt_1_lalt), .incpc(subt_1_incpc));
  orconnect orconnect_57 (.in_2(orconnect_75_out_3), .in_1(subt_1_p1), .out_3(orconnect_57_out_3));
  orconnect orconnect_58 (.in_2(orconnect_76_out_3), .in_1(subt_1_p2), .out_3(orconnect_58_out_3));
  orconnect orconnect_59 (.in_2(orconnect_77_out_3), .in_1(subt_1_p3), .out_3(orconnect_59_out_3));
  orconnect orconnect_60 (.in_2(orconnect_78_out_3), .in_1(subt_1_p4), .out_3(orconnect_60_out_3));
  orconnect orconnect_61 (.in_2(orconnect_66_out_3), .in_1(subt_1_p5), .out_3(orconnect_61_out_3));
  orconnect orconnect_62 (.in_2(orconnect_67_out_3), .in_1(subt_1_a0), .out_3(orconnect_62_out_3));
  orconnect orconnect_63 (.in_2(orconnect_68_out_3), .in_1(subt_1_a1), .out_3(orconnect_63_out_3));
  orconnect orconnect_64 (.in_2(orconnect_69_out_3), .in_1(subt_1_cr), .out_3(orconnect_64_out_3));
  orconnect orconnect_65 (.in_2(orconnect_74_out_3), .in_1(subt_1_p0), .out_3(orconnect_65_out_3));
  orconnect orconnect_66 (.in_2(orconnect_85_out_3), .in_1(valin_1_p5), .out_3(orconnect_66_out_3));
  orconnect orconnect_67 (.in_2(orconnect_86_out_3), .in_1(valin_1_a0), .out_3(orconnect_67_out_3));
  orconnect orconnect_68 (.in_2(orconnect_87_out_3), .in_1(valin_1_a1), .out_3(orconnect_68_out_3));
  orconnect orconnect_69 (.in_2(orconnect_88_out_3), .in_1(valin_1_cr), .out_3(orconnect_69_out_3));
  orconnect orconnect_70 (.in_2(orconnect_89_out_3), .in_1(valin_1_mr), .out_3(orconnect_70_out_3));
  orconnect orconnect_71 (.in_2(orconnect_79_out_3), .in_1(valin_1_mw), .out_3(orconnect_71_out_3));
  orconnect orconnect_72 (.in_2(orconnect_80_out_3), .in_1(valin_1_lalt), .out_3(orconnect_72_out_3));
  orconnect orconnect_73 (.in_2(orconnect_81_out_3), .in_1(valin_1_incpc), .out_3(orconnect_73_out_3));
  ValiN valin_1 (
    .EN(decoder_1_out5), .RingCounter(RingCounter), .P0(valin_1_p0), .P1(valin_1_p1), .P2(valin_1_p2),
    .P3(valin_1_p3), .P4(valin_1_p4), .P5(valin_1_p5), .A0(valin_1_a0), .A1(valin_1_a1), .Cr(valin_1_cr),
    .Mr(valin_1_mr), .Mw(valin_1_mw), .Lalt(valin_1_lalt), .incpc(valin_1_incpc));
  orconnect orconnect_74 (.in_2(orconnect_90_out_3), .in_1(valin_1_p0), .out_3(orconnect_74_out_3));
  orconnect orconnect_75 (.in_2(orconnect_91_out_3), .in_1(valin_1_p1), .out_3(orconnect_75_out_3));
  orconnect orconnect_76 (.in_2(orconnect_82_out_3), .in_1(valin_1_p2), .out_3(orconnect_76_out_3));
  orconnect orconnect_77 (.in_2(orconnect_83_out_3), .in_1(valin_1_p3), .out_3(orconnect_77_out_3));
  orconnect orconnect_78 (.in_2(orconnect_84_out_3), .in_1(valin_1_p4), .out_3(orconnect_78_out_3));
  orconnect orconnect_79 (.in_2(orconnect_96_out_3), .in_1(outpt_1_mw), .out_3(orconnect_79_out_3));
  orconnect orconnect_80 (.in_2(orconnect_97_out_3), .in_1(outpt_1_lalt), .out_3(orconnect_80_out_3));
  orconnect orconnect_81 (.in_2(orconnect_98_out_3), .in_1(outpt_1_incpc), .out_3(orconnect_81_out_3));
  orconnect orconnect_82 (.in_2(orconnect_101_out_3), .in_1(outpt_1_p2), .out_3(orconnect_82_out_3));
  orconnect orconnect_83 (.in_2(orconnect_102_out_3), .in_1(outpt_1_p3), .out_3(orconnect_83_out_3));
  orconnect orconnect_84 (.in_2(orconnect_103_out_3), .in_1(outpt_1_p4), .out_3(orconnect_84_out_3));
  orconnect orconnect_85 (.in_2(orconnect_104_out_3), .in_1(outpt_1_p5), .out_3(orconnect_85_out_3));
  orconnect orconnect_86 (.in_2(orconnect_92_out_3), .in_1(outpt_1_a0), .out_3(orconnect_86_out_3));
  orconnect orconnect_87 (.in_2(orconnect_93_out_3), .in_1(outpt_1_a1), .out_3(orconnect_87_out_3));
  orconnect orconnect_88 (.in_2(orconnect_94_out_3), .in_1(outpt_1_cr), .out_3(orconnect_88_out_3));
  orconnect orconnect_89 (.in_2(orconnect_95_out_3), .in_1(outpt_1_mr), .out_3(orconnect_89_out_3));
  Outpt outpt_1 (
    .EN(decoder_1_out6), .RingCounter(RingCounter), .P0(outpt_1_p0), .P1(outpt_1_p1), .P2(outpt_1_p2),
    .P3(outpt_1_p3), .P4(outpt_1_p4), .P5(outpt_1_p5), .A0(outpt_1_a0), .A1(outpt_1_a1), .Cr(outpt_1_cr),
    .Mr(outpt_1_mr), .Mw(outpt_1_mw), .Lalt(outpt_1_lalt), .incpc(outpt_1_incpc));
  orconnect orconnect_90 (.in_2(orconnect_99_out_3), .in_1(outpt_1_p0), .out_3(orconnect_90_out_3));
  orconnect orconnect_91 (.in_2(orconnect_100_out_3), .in_1(outpt_1_p1), .out_3(orconnect_91_out_3));
  orconnect orconnect_92 (.in_2(orconnect_110_out_3), .in_1(halt_1_a0), .out_3(orconnect_92_out_3));
  orconnect orconnect_93 (.in_2(orconnect_111_out_3), .in_1(halt_1_a1), .out_3(orconnect_93_out_3));
  orconnect orconnect_94 (.in_2(orconnect_112_out_3), .in_1(halt_1_cr), .out_3(orconnect_94_out_3));
  orconnect orconnect_95 (.in_2(orconnect_113_out_3), .in_1(halt_1_mr), .out_3(orconnect_95_out_3));
  orconnect orconnect_96 (.in_2(orconnect_114_out_3), .in_1(halt_1_mw), .out_3(orconnect_96_out_3));
  orconnect orconnect_97 (.in_2(orconnect_105_out_3), .in_1(halt_1_lalt), .out_3(orconnect_97_out_3));
  orconnect orconnect_98 (.in_2(orconnect_106_out_3), .in_1(halt_1_incpc), .out_3(orconnect_98_out_3));
  Halt halt_1 (
    .EN(decoder_1_out7), .RingCounter(RingCounter), .stop(STOP), .P0(halt_1_p0), .P1(halt_1_p1),
    .P2(halt_1_p2), .P3(halt_1_p3), .P4(halt_1_p4), .P5(halt_1_p5), .A0(halt_1_a0), .A1(halt_1_a1),
    .Cr(halt_1_cr), .Mr(halt_1_mr), .Mw(halt_1_mw), .Lalt(halt_1_lalt), .incpc(halt_1_incpc));
  orconnect orconnect_99 (.in_2(orconnect_115_out_3), .in_1(halt_1_p0), .out_3(orconnect_99_out_3));
  orconnect orconnect_100 (.in_2(orconnect_116_out_3), .in_1(halt_1_p1), .out_3(orconnect_100_out_3));
  orconnect orconnect_101 (.in_2(orconnect_117_out_3), .in_1(halt_1_p2), .out_3(orconnect_101_out_3));
  orconnect orconnect_102 (.in_2(orconnect_107_out_3), .in_1(halt_1_p3), .out_3(orconnect_102_out_3));
  orconnect orconnect_103 (.in_2(orconnect_108_out_3), .in_1(halt_1_p4), .out_3(orconnect_103_out_3));
  orconnect orconnect_104 (.in_2(orconnect_109_out_3), .in_1(halt_1_p5), .out_3(orconnect_104_out_3));
  orconnect orconnect_105 (.in_2(orconnect_122_out_3), .in_1(skipcon_1_lalt), .out_3(orconnect_105_out_3));
  orconnect orconnect_106 (.in_2(orconnect_123_out_3), .in_1(skipcon_1_incpc), .out_3(orconnect_106_out_3));
  orconnect orconnect_107 (.in_2(orconnect_127_out_3), .in_1(skipcon_1_p3), .out_3(orconnect_107_out_3));
  orconnect orconnect_108 (.in_2(orconnect_128_out_3), .in_1(skipcon_1_p4), .out_3(orconnect_108_out_3));
  orconnect orconnect_109 (.in_2(orconnect_129_out_3), .in_1(skipcon_1_p5), .out_3(orconnect_109_out_3));
  orconnect orconnect_110 (.in_2(orconnect_130_out_3), .in_1(skipcon_1_a0), .out_3(orconnect_110_out_3));
  orconnect orconnect_111 (.in_2(orconnect_118_out_3), .in_1(skipcon_1_a1), .out_3(orconnect_111_out_3));
  orconnect orconnect_112 (.in_2(orconnect_119_out_3), .in_1(skipcon_1_cr), .out_3(orconnect_112_out_3));
  orconnect orconnect_113 (.in_2(orconnect_120_out_3), .in_1(skipcon_1_mr), .out_3(orconnect_113_out_3));
  orconnect orconnect_114 (.in_2(orconnect_121_out_3), .in_1(skipcon_1_mw), .out_3(orconnect_114_out_3));
  skipcon skipcon_1 (
    .EN(decoder_1_out8), .RingCounter(RingCounter), .AC(AC), .data(Instruction[11:0]), .P0(skipcon_1_p0),
    .P1(skipcon_1_p1), .P2(skipcon_1_p2), .P3(skipcon_1_p3), .P4(skipcon_1_p4), .P5(skipcon_1_p5),
    .A0(skipcon_1_a0), .A1(skipcon_1_a1), .Cr(skipcon_1_cr), .Mr(skipcon_1_mr), .Mw(skipcon_1_mw),
    .Lalt(skipcon_1_lalt), .INCPC(skipcon_1_incpc));
  orconnect orconnect_115 (.in_2(orconnect_124_out_3), .in_1(skipcon_1_p0), .out_3(orconnect_115_out_3));
  orconnect orconnect_116 (.in_2(orconnect_125_out_3), .in_1(skipcon_1_p1), .out_3(orconnect_116_out_3));
  orconnect orconnect_117 (.in_2(orconnect_126_out_3), .in_1(skipcon_1_p2), .out_3(orconnect_117_out_3));
  orconnect orconnect_118 (.in_2(orconnect_135_out_3), .in_1(jump_1_a1), .out_3(orconnect_118_out_3));
  orconnect orconnect_119 (.in_2(orconnect_136_out_3), .in_1(jump_1_cr), .out_3(orconnect_119_out_3));
  orconnect orconnect_120 (.in_2(orconnect_137_out_3), .in_1(jump_1_mr), .out_3(orconnect_120_out_3));
  orconnect orconnect_121 (.in_2(orconnect_138_out_3), .in_1(jump_1_mw), .out_3(orconnect_121_out_3));
  orconnect orconnect_122 (.in_2(orconnect_139_out_3), .in_1(jump_1_lalt), .out_3(orconnect_122_out_3));
  orconnect orconnect_123 (.in_2(orconnect_131_out_3), .in_1(jump_1_incpc), .out_3(orconnect_123_out_3));
  Jump jump_1 (
    .EN(decoder_1_out9), .RingCounter(RingCounter), .P0(jump_1_p0), .P1(jump_1_p1), .P2(jump_1_p2),
    .P3(jump_1_p3), .P4(jump_1_p4), .P5(jump_1_p5), .A0(jump_1_a0), .A1(jump_1_a1), .Cr(jump_1_cr),
    .Mr(jump_1_mr), .Mw(jump_1_mw), .Lalt(jump_1_lalt), .incpc(jump_1_incpc));
  orconnect orconnect_124 (.in_2(orconnect_140_out_3), .in_1(jump_1_p0), .out_3(orconnect_124_out_3));
  orconnect orconnect_125 (.in_2(orconnect_141_out_3), .in_1(jump_1_p1), .out_3(orconnect_125_out_3));
  orconnect orconnect_126 (.in_2(orconnect_142_out_3), .in_1(jump_1_p2), .out_3(orconnect_126_out_3));
  orconnect orconnect_127 (.in_2(orconnect_143_out_3), .in_1(jump_1_p3), .out_3(orconnect_127_out_3));
  orconnect orconnect_128 (.in_2(orconnect_132_out_3), .in_1(jump_1_p4), .out_3(orconnect_128_out_3));
  orconnect orconnect_129 (.in_2(orconnect_133_out_3), .in_1(jump_1_p5), .out_3(orconnect_129_out_3));
  orconnect orconnect_130 (.in_2(orconnect_134_out_3), .in_1(jump_1_a0), .out_3(orconnect_130_out_3));
  orconnect orconnect_131 (.in_2(orconnect_148_out_3), .in_1(clear_1_incpc), .out_3(orconnect_131_out_3));
  orconnect orconnect_132 (.in_2(orconnect_153_out_3), .in_1(clear_1_p4), .out_3(orconnect_132_out_3));
  orconnect orconnect_133 (.in_2(orconnect_154_out_3), .in_1(clear_1_p5), .out_3(orconnect_133_out_3));
  orconnect orconnect_134 (.in_2(orconnect_155_out_3), .in_1(clear_1_a0), .out_3(orconnect_134_out_3));
  orconnect orconnect_135 (.in_2(orconnect_156_out_3), .in_1(clear_1_a1), .out_3(orconnect_135_out_3));
  orconnect orconnect_136 (.in_2(orconnect_144_out_3), .in_1(clear_1_cr), .out_3(orconnect_136_out_3));
  orconnect orconnect_137 (.in_2(orconnect_145_out_3), .in_1(clear_1_mr), .out_3(orconnect_137_out_3));
  orconnect orconnect_138 (.in_2(orconnect_146_out_3), .in_1(clear_1_mw), .out_3(orconnect_138_out_3));
  orconnect orconnect_139 (.in_2(orconnect_147_out_3), .in_1(clear_1_lalt), .out_3(orconnect_139_out_3));
  clear clear_1 (
    .EN(decoder_1_out10), .RingCounter(RingCounter), .P0(clear_1_p0), .P1(clear_1_p1), .P2(clear_1_p2),
    .P3(clear_1_p3), .P4(clear_1_p4), .P5(clear_1_p5), .A0(clear_1_a0), .A1(clear_1_a1), .Cr(clear_1_cr),
    .Mr(clear_1_mr), .Mw(clear_1_mw), .Lalt(clear_1_lalt), .incpc(clear_1_incpc));
  orconnect orconnect_140 (.in_2(orconnect_149_out_3), .in_1(clear_1_p0), .out_3(orconnect_140_out_3));
  orconnect orconnect_141 (.in_2(orconnect_150_out_3), .in_1(clear_1_p1), .out_3(orconnect_141_out_3));
  orconnect orconnect_142 (.in_2(orconnect_151_out_3), .in_1(clear_1_p2), .out_3(orconnect_142_out_3));
  orconnect orconnect_143 (.in_2(orconnect_152_out_3), .in_1(clear_1_p3), .out_3(orconnect_143_out_3));
  orconnect orconnect_144 (.in_2(orconnect_162_out_3), .in_1(addi_1_cr), .out_3(orconnect_144_out_3));
  orconnect orconnect_145 (.in_2(orconnect_163_out_3), .in_1(addi_1_mr), .out_3(orconnect_145_out_3));
  orconnect orconnect_146 (.in_2(orconnect_164_out_3), .in_1(addi_1_mw), .out_3(orconnect_146_out_3));
  orconnect orconnect_147 (.in_2(orconnect_165_out_3), .in_1(addi_1_lalt), .out_3(orconnect_147_out_3));
  orconnect orconnect_148 (.in_2(orconnect_157_out_3), .in_1(addi_1_incpc), .out_3(orconnect_148_out_3));
  AddI addi_1 (
    .EN(decoder_1_out11), .RingCounter(RingCounter), .P0(addi_1_p0), .P1(addi_1_p1), .P2(addi_1_p2),
    .P3(addi_1_p3), .P4(addi_1_p4), .P5(addi_1_p5), .A0(addi_1_a0), .A1(addi_1_a1), .Cr(addi_1_cr),
    .Mr(addi_1_mr), .Mw(addi_1_mw), .Lalt(addi_1_lalt), .incpc(addi_1_incpc));
  orconnect orconnect_149 (.in_2(orconnect_166_out_3), .in_1(addi_1_p0), .out_3(orconnect_149_out_3));
  orconnect orconnect_150 (.in_2(orconnect_167_out_3), .in_1(addi_1_p1), .out_3(orconnect_150_out_3));
  orconnect orconnect_151 (.in_2(orconnect_168_out_3), .in_1(addi_1_p2), .out_3(orconnect_151_out_3));
  orconnect orconnect_152 (.in_2(orconnect_169_out_3), .in_1(addi_1_p3), .out_3(orconnect_152_out_3));
  orconnect orconnect_153 (.in_2(orconnect_158_out_3), .in_1(addi_1_p4), .out_3(orconnect_153_out_3));
  orconnect orconnect_154 (.in_2(orconnect_159_out_3), .in_1(addi_1_p5), .out_3(orconnect_154_out_3));
  orconnect orconnect_155 (.in_2(orconnect_160_out_3), .in_1(addi_1_a0), .out_3(orconnect_155_out_3));
  orconnect orconnect_156 (.in_2(orconnect_161_out_3), .in_1(addi_1_a1), .out_3(orconnect_156_out_3));
  orconnect orconnect_157 (.in_2(orconnect_174_out_3), .in_1(jumpi_1_incpc), .out_3(orconnect_157_out_3));
  orconnect orconnect_158 (.in_2(orconnect_179_out_3), .in_1(jumpi_1_p4), .out_3(orconnect_158_out_3));
  orconnect orconnect_159 (.in_2(orconnect_180_out_3), .in_1(jumpi_1_p5), .out_3(orconnect_159_out_3));
  orconnect orconnect_160 (.in_2(orconnect_181_out_3), .in_1(jumpi_1_a0), .out_3(orconnect_160_out_3));
  orconnect orconnect_161 (.in_2(orconnect_182_out_3), .in_1(jumpi_1_a1), .out_3(orconnect_161_out_3));
  orconnect orconnect_162 (.in_2(orconnect_170_out_3), .in_1(jumpi_1_cr), .out_3(orconnect_162_out_3));
  orconnect orconnect_163 (.in_2(orconnect_171_out_3), .in_1(jumpi_1_mr), .out_3(orconnect_163_out_3));
  orconnect orconnect_164 (.in_2(orconnect_172_out_3), .in_1(jumpi_1_mw), .out_3(orconnect_164_out_3));
  orconnect orconnect_165 (.in_2(orconnect_173_out_3), .in_1(jumpi_1_lalt), .out_3(orconnect_165_out_3));
  JumpI jumpi_1 (
    .EN(decoder_1_out12), .RingCounter(RingCounter), .P0(jumpi_1_p0), .P1(jumpi_1_p1), .P2(jumpi_1_p2),
    .P3(jumpi_1_p3), .P4(jumpi_1_p4), .P5(jumpi_1_p5), .A0(jumpi_1_a0), .A1(jumpi_1_a1), .Cr(jumpi_1_cr),
    .Mr(jumpi_1_mr), .Mw(jumpi_1_mw), .Lalt(jumpi_1_lalt), .incpc(jumpi_1_incpc));
  orconnect orconnect_166 (.in_2(orconnect_175_out_3), .in_1(jumpi_1_p0), .out_3(orconnect_166_out_3));
  orconnect orconnect_167 (.in_2(orconnect_176_out_3), .in_1(jumpi_1_p1), .out_3(orconnect_167_out_3));
  orconnect orconnect_168 (.in_2(orconnect_177_out_3), .in_1(jumpi_1_p2), .out_3(orconnect_168_out_3));
  orconnect orconnect_169 (.in_2(orconnect_178_out_3), .in_1(jumpi_1_p3), .out_3(orconnect_169_out_3));
  orconnect orconnect_170 (.in_2(orconnect_186_out_3), .in_1(loadi_1_cr), .out_3(orconnect_170_out_3));
  orconnect orconnect_171 (.in_2(orconnect_187_out_3), .in_1(loadi_1_mr), .out_3(orconnect_171_out_3));
  orconnect orconnect_172 (.in_2(orconnect_188_out_3), .in_1(loadi_1_mw), .out_3(orconnect_172_out_3));
  orconnect orconnect_173 (.in_2(orconnect_189_out_3), .in_1(loadi_1_lalt), .out_3(orconnect_173_out_3));
  orconnect orconnect_174 (.in_2(orconnect_190_out_3), .in_1(loadi_1_incpc), .out_3(orconnect_174_out_3));
  LoadI loadi_1 (
    .EN(decoder_1_out13), .RingCounter(RingCounter), .P0(loadi_1_p0), .P1(loadi_1_p1), .P2(loadi_1_p2),
    .P3(loadi_1_p3), .P4(loadi_1_p4), .P5(loadi_1_p5), .A0(loadi_1_a0), .A1(loadi_1_a1), .Cr(loadi_1_cr),
    .Mr(loadi_1_mr), .Mw(loadi_1_mw), .Lalt(loadi_1_lalt), .incpc(loadi_1_incpc));
  orconnect orconnect_175 (.in_2(orconnect_191_out_3), .in_1(loadi_1_p0), .out_3(orconnect_175_out_3));
  orconnect orconnect_176 (.in_2(orconnect_192_out_3), .in_1(loadi_1_p1), .out_3(orconnect_176_out_3));
  orconnect orconnect_177 (.in_2(orconnect_193_out_3), .in_1(loadi_1_p2), .out_3(orconnect_177_out_3));
  orconnect orconnect_178 (.in_2(orconnect_194_out_3), .in_1(loadi_1_p3), .out_3(orconnect_178_out_3));
  orconnect orconnect_179 (.in_2(orconnect_195_out_3), .in_1(loadi_1_p4), .out_3(orconnect_179_out_3));
  orconnect orconnect_180 (.in_2(orconnect_183_out_3), .in_1(loadi_1_p5), .out_3(orconnect_180_out_3));
  orconnect orconnect_181 (.in_2(orconnect_184_out_3), .in_1(loadi_1_a0), .out_3(orconnect_181_out_3));
  orconnect orconnect_182 (.in_2(orconnect_185_out_3), .in_1(loadi_1_a1), .out_3(orconnect_182_out_3));
  orconnect orconnect_183 (.in_2(teststartload_1_p5), .in_1(storei_1_p5), .out_3(orconnect_183_out_3));
  orconnect orconnect_184 (.in_2(teststartload_1_a0), .in_1(storei_1_a0), .out_3(orconnect_184_out_3));
  orconnect orconnect_185 (.in_2(teststartload_1_a1), .in_1(storei_1_a1), .out_3(orconnect_185_out_3));
  orconnect orconnect_186 (.in_2(teststartload_1_cr), .in_1(storei_1_cr), .out_3(orconnect_186_out_3));
  orconnect orconnect_187 (.in_2(teststartload_1_mr), .in_1(storei_1_mr), .out_3(orconnect_187_out_3));
  orconnect orconnect_188 (.in_2(teststartload_1_mw), .in_1(storei_1_mw), .out_3(orconnect_188_out_3));
  orconnect orconnect_189 (.in_2(teststartload_1_lalt), .in_1(storei_1_lalt), .out_3(orconnect_189_out_3));
  orconnect orconnect_190 (.in_1(storei_1_incpc), .out_3(orconnect_190_out_3));  // open: in_2
  StoreI storei_1 (
    .EN(decoder_1_out14), .RingCounter(RingCounter), .P0(storei_1_p0), .P1(storei_1_p1), .P2(storei_1_p2),
    .P3(storei_1_p3), .P4(storei_1_p4), .P5(storei_1_p5), .A0(storei_1_a0), .A1(storei_1_a1),
    .Cr(storei_1_cr), .Mr(storei_1_mr), .Mw(storei_1_mw), .Lalt(storei_1_lalt), .incpc(storei_1_incpc));
  orconnect orconnect_191 (.in_2(teststartload_1_p0), .in_1(storei_1_p0), .out_3(orconnect_191_out_3));
  orconnect orconnect_192 (.in_2(teststartload_1_p1), .in_1(storei_1_p1), .out_3(orconnect_192_out_3));
  orconnect orconnect_193 (.in_2(teststartload_1_p2), .in_1(storei_1_p2), .out_3(orconnect_193_out_3));
  orconnect orconnect_194 (.in_2(teststartload_1_p3), .in_1(storei_1_p3), .out_3(orconnect_194_out_3));
  orconnect orconnect_195 (.in_2(teststartload_1_p4), .in_1(storei_1_p4), .out_3(orconnect_195_out_3));
  TESTSTARTLOAD teststartload_1 (
    .EN(decoder_1_out15), .RingCounter(RingCounter), .P0(teststartload_1_p0), .P1(teststartload_1_p1),
    .P2(teststartload_1_p2), .P3(teststartload_1_p3), .P4(teststartload_1_p4), .P5(teststartload_1_p5),
    .A0(teststartload_1_a0), .A1(teststartload_1_a1), .Cr(teststartload_1_cr), .Mr(teststartload_1_mr),
    .Mw(teststartload_1_mw), .Lalt(teststartload_1_lalt));

  // Notes on the sheet:
  //   Instruction: initial=0x3021
  //   P0
  //   P1
  //   P2
  //   P3
  //   P4
  //   P5
  //   A0
  //   A1
  //   Cr
  //   Mr
  //   Mw
  //   Lalt
endmodule

module Add (
  input  En,
  input  [7:0] RingCounter,
  output P0,
  output P1,
  output P2,
  output P3,
  output P4,
  output P5,
  output A0,
  output A1,
  output Cr,
  output Mr,
  output Mw,
  output Lalt,
  output incpc
);

  wire and_2_out, and_5_out, and_6_out;

  and and_1 (P0, RingCounter[3], En);
  or or_1 (P1, P0, incpc, and_5_out);
  and and_2 (and_2_out, RingCounter[4], En);
  and and_3 (A0, En, RingCounter[5]);
  or out3 (P3, P0, and_5_out, and_6_out, and_2_out);
  and and_4 (Cr, RingCounter[7], En);
  or or_2 (P4, and_6_out, incpc, and_2_out);
  or or_3 (P5, and_6_out, A0);
  and and_5 (and_5_out, RingCounter[0], En);
  and and_6 (and_6_out, RingCounter[1], En);
  or or_4 (Mr, and_2_out, and_6_out);
  and and_7 (incpc, RingCounter[2], En);

  assign A1 = 1'b0;
  assign Lalt = A0;
  assign Mw = 1'b0;
  assign P2 = P0;

  // Notes on the sheet:
  //   In - register - Out
  //   3 -   MAR    - 0
  //   4 -     PC     - 1
  //   3,4 -  MBR  - 0,1
  //   5 -     AC     - 2
  //   5,3 - InReg - 2,0
  //   5,4 - OutReg - 2,1
  //   5,4,3 -  IR  - 2,1,0
  //   ADD=0011
endmodule

module BaseOp (
  input  EN,
  input  [7:0] RingCounter,
  output P0,
  output P1,
  output P2,
  output P3,
  output P4,
  output P5,
  output A0,
  output A1,
  output Cr,
  output Mr,
  output Mw,
  output Lalt,
  output IncPC
);

  wire and_1_out, and_5_out, and_6_out, and_7_out, and_8_out, and_9_out;

  and and_1 (and_1_out, RingCounter[0], EN);
  and and_2 (Mr, RingCounter[1], EN);
  or or_1 (P1, and_1_out, IncPC);
  and and_3 (IncPC, RingCounter[2], EN);
  // AND_Gate and_4 has open pins: in0=RingCounter[3], in1=EN, out=open
  or or_2 (P3, and_1_out, Mr);
  and and_5 (and_5_out, RingCounter[4], EN);
  or or_3 (P4, Mr, IncPC);
  and and_6 (and_6_out, RingCounter[5], EN);
  and and_7 (and_7_out, RingCounter[6], EN);
  and and_8 (and_8_out, RingCounter[7], EN);
  buf and_9 (and_9_out, EN);  // AND_Gate
  or or_4 (Cr, and_5_out, and_6_out, and_7_out, and_8_out, and_9_out);

  assign P5 = Mr;

  // Notes on the sheet:
  //   In - register - Out
  //   3 -   MAR    - 0
  //   4 -     PC     - 1
  //   3,4 -  MBR  - 0,1
  //   5 -     AC     - 2
  //   5,3 - InReg - 2,0
  //   5,4 - OutReg - 2,1
  //   5,4,3 -  IR  - 2,1,0
endmodule

module Load (
  input  EN,
  input  [7:0] RingCounter,
  output P0,
  output P1,
  output P2,
  output P3,
  output P4,
  output P5,
  output A0,
  output A1,
  output Cr,
  output Mr,
  output Mw,
  output Lalt,
  output incpc
);

  wire and_1_out, and_2_out, and_5_out, and_7_out, and_8_out;

  and and_1 (and_1_out, RingCounter[0], EN);
  and and_2 (and_2_out, RingCounter[1], EN);
  or or_1 (P1, and_1_out, P0, incpc);
  and and_3 (incpc, RingCounter[2], EN);
  and and_4 (P0, RingCounter[3], EN);
  or or_2 (P3, and_1_out, P0, and_2_out);
  and and_5 (and_5_out, RingCounter[4], EN);
  or or_3 (P4, and_2_out, incpc);
  // AND_Gate and_6 has open pins: in0=RingCounter[5], in1=EN, out=open
  or or_4 (P5, and_2_out, and_5_out);
  and and_7 (and_7_out, RingCounter[6], EN);
  and and_8 (and_8_out, RingCounter[7], EN);
  or or_5 (Cr, and_7_out, and_8_out);
  or or_6 (Mr, and_2_out, and_5_out);

  assign A0 = 1'b0;
  assign A1 = 1'b0;
  assign Lalt = 1'b0;
  assign Mw = 1'b0;
  assign P2 = P0;
endmodule

module ALU (
  input  [15:0] ACi,
  input  [15:0] MBR,
  input  A0,
  input  A1,
  output Zero,
  output Carry,
  output Negative,
  output [15:0] ACo
);

  wire and_1_out, and_2_out, comparator_1_eq, comparator_1_gt, comparator_1_lt, comparator_2_eq,
       comparator_2_gt, comparator_2_lt, controlled_buffer_1_out, controlled_buffer_2_out, or_1_out;
  wire [15:0] adder_1_out, controlled_buffer_3_out, subtractor_1_out;

  or or_1 (or_1_out, A1, A0);
  assign controlled_buffer_1_out = or_1_out ? A1 : 1'bz;  // Controlled_Buffer controlled_buffer_1
  Comparator #(.width(1)) comparator_1 (
    .a(controlled_buffer_1_out), .b(controlled_buffer_2_out), .gt(comparator_1_gt), .eq(comparator_1_eq),
    .lt(comparator_1_lt));
  assign controlled_buffer_2_out = or_1_out ? A0 : 1'bz;  // Controlled_Buffer controlled_buffer_2
  and and_1 (and_1_out, ~A0, ~A1);  // AND_Gate
  Comparator #(.width(16)) comparator_2 (
    .a(MBR), .b(ACi), .gt(comparator_2_gt), .eq(comparator_2_eq), .lt(comparator_2_lt));
  assign controlled_buffer_3_out = comparator_1_gt ? adder_1_out : 16'bz;  // Controlled_Buffer controlled_buffer_3
  Adder #(.width(16)) adder_1 (.a(ACi), .b(MBR), .out(adder_1_out), .cout(Carry));  // open: cin
  assign controlled_buffer_3_out = comparator_1_lt ? subtractor_1_out : 16'bz;  // Controlled_Buffer controlled_buffer_4
  Subtractor #(.width(16)) subtractor_1 (.a(ACi), .b(MBR), .out(subtractor_1_out));  // open: bin, bout
  Merger merger_1 (.Busin(controlled_buffer_3_out), .DataIn({16{1'b0}}), .switch(and_1_out), .outp(ACo));
  assign controlled_buffer_3_out = comparator_1_eq ? {16{1'b0}} : 16'bz;  // Controlled_Buffer controlled_buffer_5
  and and_2 (and_2_out, comparator_2_eq, comparator_1_lt);
  or or_2 (Zero, and_2_out, comparator_1_eq);
  and and_3 (Negative, comparator_2_gt, comparator_1_lt);
endmodule

module orconnect (
  input  in_1,
  input  in_2,
  output out_3
);

  or or_1 (out_3, in_1, in_2);
endmodule

module toggle (
  input  [15:0] i,
  input  T,
  output [15:0] o1,
  output [15:0] o2
);

  wire not_1_out;

  not not_1 (not_1_out, T);
  assign o1 = not_1_out ? i : 16'bz;  // Controlled_Buffer controlled_buffer_1
  assign o2 = T ? i : 16'bz;  // Controlled_Buffer controlled_buffer_2
endmodule

module TESTSTARTLOAD (
  input  EN,
  input  [7:0] RingCounter,
  output P0,
  output P1,
  output P2,
  output P3,
  output P4,
  output P5,
  output A0,
  output A1,
  output Cr,
  output Mr,
  output Mw,
  output Lalt
);

  wire or_1_out;

  or or_1 (or_1_out, RingCounter[0], RingCounter[1], RingCounter[2], RingCounter[3], RingCounter[4], RingCounter[5], RingCounter[6], RingCounter[7]);
  and and_1 (P0, or_1_out, EN);

  assign A0 = 1'b0;
  assign A1 = 1'b0;
  assign Cr = 1'b0;
  assign Lalt = 1'b0;
  assign Mr = 1'b0;
  assign Mw = 1'b0;
  assign P1 = P0;
  assign P2 = P0;
  assign P3 = P0;
  assign P4 = P0;
  assign P5 = P0;
endmodule

module Merger (
  input  [15:0] Busin,
  input  switch,
  input  [15:0] DataIn,
  output [15:0] outp
);

  wire not_1_out;

  not not_1 (not_1_out, switch);
  assign outp = not_1_out ? Busin : 16'bz;  // Controlled_Buffer controlled_buffer_1
  assign outp = switch ? DataIn : 16'bz;  // Controlled_Buffer controlled_buffer_2
endmodule

module Store (
  input  EN,
  input  [7:0] RingCounter,
  output P0,
  output P1,
  output P2,
  output P3,
  output P4,
  output P5,
  output A0,
  output A1,
  output Cr,
  output Mr,
  output Mw,
  output Lalt,
  output incpc
);

  wire and_1_out, and_7_out, and_8_out;

  and and_1 (and_1_out, RingCounter[0], EN);
  and and_2 (Mr, RingCounter[1], EN);
  or or_1 (P1, and_1_out, P0, incpc);
  and and_3 (incpc, RingCounter[2], EN);
  or or_2 (P2, P0, Mw);
  and and_4 (P0, RingCounter[3], EN);
  or or_3 (P3, and_1_out, P0, Mr);
  and and_5 (Mw, RingCounter[4], EN);
  or or_4 (P4, Mr, incpc);
  // AND_Gate and_6 has open pins: in0=RingCounter[5], in1=EN, out=open
  and and_7 (and_7_out, RingCounter[6], EN);
  and and_8 (and_8_out, RingCounter[7], EN);
  or or_5 (Cr, and_7_out, and_8_out);

  assign P5 = Mr;

  // Notes on the sheet:
  //   In - register - Out
  //   3 -   MAR    - 0
  //   4 -     PC     - 1
  //   3,4 -  MBR  - 0,1
  //   5 -     AC     - 2
  //   5,3 - InReg - 2,0
  //   5,4 - OutReg - 2,1
  //   5,4,3 -  IR  - 2,1,0
endmodule

module subt (
  input  En,
  input  [7:0] RingCounter,
  output P0,
  output P1,
  output P2,
  output P3,
  output P4,
  output P5,
  output A0,
  output A1,
  output Cr,
  output Mr,
  output Mw,
  output Lalt,
  output incpc
);

  wire and_2_out, and_5_out, and_6_out;

  and and_1 (P0, RingCounter[3], En);
  or or_1 (P1, P0, incpc, and_5_out);
  and and_2 (and_2_out, RingCounter[4], En);
  and and_3 (A1, En, RingCounter[5]);
  or out3 (P3, P0, and_5_out, and_6_out, and_2_out);
  and and_4 (Cr, RingCounter[7], En);
  or or_2 (P4, and_6_out, incpc, and_2_out);
  or or_3 (P5, and_6_out, A1);
  and and_5 (and_5_out, RingCounter[0], En);
  and and_6 (and_6_out, RingCounter[1], En);
  or or_4 (Mr, and_2_out, and_6_out);
  and and_7 (incpc, RingCounter[2], En);

  assign A0 = 1'b0;
  assign Lalt = A1;
  assign Mw = 1'b0;
  assign P2 = P0;

  // Notes on the sheet:
  //   ADD=0011
endmodule

module ValiN (
  input  EN,
  input  [7:0] RingCounter,
  output P0,
  output P1,
  output P2,
  output P3,
  output P4,
  output P5,
  output A0,
  output A1,
  output Cr,
  output Mr,
  output Mw,
  output Lalt,
  output incpc
);

  wire and_1_out, and_6_out, and_7_out, and_8_out;

  and and_1 (and_1_out, RingCounter[0], EN);
  and and_2 (Mr, RingCounter[1], EN);
  or or_1 (P1, and_1_out, incpc);
  and and_3 (incpc, RingCounter[2], EN);
  and and_4 (P0, RingCounter[3], EN);
  or or_2 (P3, and_1_out, Mr);
  // AND_Gate and_5 has open pins: in0=RingCounter[4], in1=EN, out=open
  or or_3 (P4, Mr, incpc);
  and and_6 (and_6_out, RingCounter[5], EN);
  or or_4 (P5, Mr, P0);
  and and_7 (and_7_out, RingCounter[6], EN);
  and and_8 (and_8_out, RingCounter[7], EN);
  or or_5 (Cr, and_6_out, and_7_out, and_8_out);

  assign P2 = P0;

  // Notes on the sheet:
  //   In - register - Out
  //   3 -   MAR    - 0
  //   4 -     PC     - 1
  //   3,4 -  MBR  - 0,1
  //   5 -     AC     - 2
  //   5,3 - InReg - 2,0
  //   5,4 - OutReg - 2,1
  //   5,4,3 -  IR  - 2,1,0
endmodule

module Outpt (
  input  EN,
  input  [7:0] RingCounter,
  output P0,
  output P1,
  output P2,
  output P3,
  output P4,
  output P5,
  output A0,
  output A1,
  output Cr,
  output Mr,
  output Mw,
  output Lalt,
  output incpc
);

  wire and_1_out, and_6_out, and_7_out, and_8_out;

  and and_1 (and_1_out, RingCounter[0], EN);
  and and_2 (Mr, RingCounter[1], EN);
  or or_1 (P1, and_1_out, incpc);
  and and_3 (incpc, RingCounter[2], EN);
  and and_4 (P2, RingCounter[3], EN);
  or or_2 (P3, and_1_out, Mr);
  // AND_Gate and_5 has open pins: in0=RingCounter[4], in1=EN, out=open
  or or_3 (P4, Mr, P2, incpc);
  and and_6 (and_6_out, RingCounter[5], EN);
  or or_4 (P5, Mr, P2);
  and and_7 (and_7_out, RingCounter[6], EN);
  and and_8 (and_8_out, RingCounter[7], EN);
  or or_5 (Cr, and_6_out, and_7_out, and_8_out);
endmodule

module Halt (
  input  EN,
  input  [7:0] RingCounter,
  output stop,
  output P0,
  output P1,
  output P2,
  output P3,
  output P4,
  output P5,
  output A0,
  output A1,
  output Cr,
  output Mr,
  output Mw,
  output Lalt,
  output incpc
);


  assign A0 = 1'b0;
  assign A1 = 1'b0;
  assign Cr = 1'b0;
  assign incpc = 1'b0;
  assign Lalt = 1'b0;
  assign Mr = 1'b0;
  assign Mw = 1'b0;
  assign P0 = 1'b0;
  assign P1 = 1'b0;
  assign P2 = 1'b0;
  assign P3 = 1'b0;
  assign P4 = 1'b0;
  assign P5 = 1'b0;
  assign stop = EN;
endmodule

module enClock (
  input  toggle,
  output Cl
);

  wire clock_1_out, t_ff_1_q;

  Clock clock_1 (.out(clock_1_out));
  assign Cl = t_ff_1_q ? clock_1_out : 1'bz;  // Controlled_Buffer controlled_buffer_1
  T_Flip_Flop t_ff_1 (.clk(clock_1_out), .T(toggle), .Q(t_ff_1_q));  // open: Qn, preset, reset
endmodule

module Jump (
  input  EN,
  input  [7:0] RingCounter,
  output P0,
  output P1,
  output P2,
  output P3,
  output P4,
  output P5,
  output A0,
  output A1,
  output Cr,
  output Mr,
  output Mw,
  output Lalt,
  output incpc
);

  wire and_1_out, and_6_out, and_7_out, and_8_out;

  and and_1 (and_1_out, RingCounter[0], EN);
  and and_2 (Mr, RingCounter[1], EN);
  or or_1 (P1, and_1_out, P0, incpc);
  and and_3 (incpc, RingCounter[2], EN);
  and and_4 (P0, RingCounter[3], EN);
  or or_2 (P3, and_1_out, Mr);
  // AND_Gate and_5 has open pins: in0=RingCounter[4], in1=EN, out=open
  or or_3 (P4, Mr, P0, incpc);
  and and_6 (and_6_out, RingCounter[5], EN);
  and and_7 (and_7_out, RingCounter[6], EN);
  and and_8 (and_8_out, RingCounter[7], EN);
  or or_4 (Cr, and_6_out, and_7_out, and_8_out);

  assign P2 = P0;
  assign P5 = Mr;
endmodule

module skipcon (
  input  EN,
  input  [7:0] RingCounter,
  input  [15:0] AC,
  input  [11:0] data,
  output P0,
  output P1,
  output P2,
  output P3,
  output P4,
  output P5,
  output A0,
  output A1,
  output Cr,
  output Mr,
  output Mw,
  output Lalt,
  output INCPC
);

  wire and_1_out, and_3_out, and_4_out, and_6_out, and_7_out, and_8_out, skplogic_1_skip;

  skplogic skplogic_1 (.b11(data[11]), .b10(data[10]), .AC(AC), .skip(skplogic_1_skip));
  and and_1 (and_1_out, RingCounter[0], EN);
  and and_2 (Mr, RingCounter[1], EN);
  or or_1 (P1, and_1_out, and_4_out, and_3_out);
  and and_3 (and_3_out, RingCounter[2], EN);
  and and_4 (and_4_out, RingCounter[3], skplogic_1_skip, EN);
  or or_2 (P3, and_1_out, Mr);
  // AND_Gate and_5 has open pins: in0=RingCounter[4], in1=EN, out=open
  or or_3 (P4, Mr, and_4_out, and_3_out);
  and and_6 (and_6_out, RingCounter[5], EN);
  and and_7 (and_7_out, RingCounter[6], EN);
  and and_8 (and_8_out, RingCounter[7], EN);
  or or_4 (Cr, and_6_out, and_7_out, and_8_out);
  or or_5 (INCPC, and_3_out, and_4_out);

  assign P5 = Mr;

  // Notes on the sheet:
  //   In - register - Out
  //   3 -   MAR    - 0
  //   4 -     PC     - 1
  //   3,4 -  MBR  - 0,1
  //   5 -     AC     - 2
  //   5,3 - InReg - 2,0
  //   5,4 - OutReg - 2,1
  //   5,4,3 -  IR  - 2,1,0
endmodule

module clear (
  input  EN,
  input  [7:0] RingCounter,
  output P0,
  output P1,
  output P2,
  output P3,
  output P4,
  output P5,
  output A0,
  output A1,
  output Cr,
  output Mr,
  output Mw,
  output Lalt,
  output incpc
);

  wire and_1_out, and_7_out, and_8_out;

  and and_1 (and_1_out, RingCounter[0], EN);
  and and_2 (Mr, RingCounter[1], EN);
  or or_1 (P1, and_1_out, incpc);
  and and_3 (incpc, RingCounter[2], EN);
  and and_4 (P2, RingCounter[3], EN);
  or or_2 (P3, and_1_out, P2, Mr);
  and and_5 (A1, RingCounter[4], EN);
  or or_3 (P4, Mr, P2, incpc);
  // AND_Gate and_6 has open pins: in0=RingCounter[5], in1=EN, out=open
  or or_4 (P5, Mr, A1);
  and and_7 (and_7_out, RingCounter[6], EN);
  and and_8 (and_8_out, RingCounter[7], EN);
  or or_5 (Cr, and_7_out, and_8_out);

  assign Lalt = A1;

  // Notes on the sheet:
  //   In - register - Out
  //   3 -   MAR    - 0
  //   4 -     PC     - 1
  //   3,4 -  MBR  - 0,1
  //   5 -     AC     - 2
  //   5,3 - InReg - 2,0
  //   5,4 - OutReg - 2,1
  //   5,4,3 -  IR  - 2,1,0
endmodule

module AddI (
  input  EN,
  input  [7:0] RingCounter,
  output P0,
  output P1,
  output P2,
  output P3,
  output P4,
  output P5,
  output A0,
  output A1,
  output Cr,
  output Mr,
  output Mw,
  output Lalt,
  output incpc
);

  wire and_1_out, and_2_out, and_5_out, and_6_out;

  and and_1 (and_1_out, RingCounter[0], EN);
  and and_2 (and_2_out, RingCounter[1], EN);
  or or_1 (P1, and_1_out, P0, incpc);
  and and_3 (incpc, RingCounter[2], EN);
  and and_4 (P0, RingCounter[3], EN);
  or or_2 (P3, and_1_out, P0, and_5_out, and_6_out, and_2_out);
  and and_5 (and_5_out, RingCounter[4], EN);
  or or_3 (P4, and_2_out, and_6_out, incpc);
  and and_6 (and_6_out, RingCounter[5], EN);
  or or_4 (P5, and_2_out, A0);
  and and_7 (A0, RingCounter[6], EN);
  // AND_Gate and_8 has open pins: in0=RingCounter[7], in1=EN, out=open
  buf and_9 (Cr, EN);  // AND_Gate
  or or_5 (Mr, and_2_out, and_6_out, and_5_out);

  assign Lalt = A0;
  assign P2 = P0;

  // Notes on the sheet:
  //   In - register - Out
  //   3 -   MAR    - 0
  //   4 -     PC     - 1
  //   3,4 -  MBR  - 0,1
  //   5 -     AC     - 2
  //   5,3 - InReg - 2,0
  //   5,4 - OutReg - 2,1
  //   5,4,3 -  IR  - 2,1,0
endmodule

module JumpI (
  input  EN,
  input  [7:0] RingCounter,
  output P0,
  output P1,
  output P2,
  output P3,
  output P4,
  output P5,
  output A0,
  output A1,
  output Cr,
  output Mr,
  output Mw,
  output Lalt,
  output incpc
);

  wire and_1_out, and_5_out, and_6_out, and_8_out, and_9_out;

  and and_1 (and_1_out, RingCounter[0], EN);
  and and_2 (P5, RingCounter[1], EN);
  or or_1 (P1, and_1_out, P0, incpc);
  and and_3 (incpc, RingCounter[2], EN);
  and and_4 (P0, RingCounter[3], EN);
  or or_2 (P3, and_1_out, P0, and_5_out, P5);
  and and_5 (and_5_out, RingCounter[4], EN);
  or or_3 (P4, P5, and_6_out, incpc);
  and and_6 (and_6_out, RingCounter[5], EN);
  // AND_Gate and_7 has open pins: in0=RingCounter[6], in1=EN, out=open
  and and_8 (and_8_out, RingCounter[7], EN);
  buf and_9 (and_9_out, EN);  // AND_Gate
  or or_4 (Cr, and_8_out, and_9_out);
  or or_5 (Mr, P5, and_5_out, and_6_out);

  assign P2 = P0;

  // Notes on the sheet:
  //   In - register - Out
  //   3 -   MAR    - 0
  //   4 -     PC     - 1
  //   3,4 -  MBR  - 0,1
  //   5 -     AC     - 2
  //   5,3 - InReg - 2,0
  //   5,4 - OutReg - 2,1
  //   5,4,3 -  IR  - 2,1,0
endmodule

module LoadI (
  input  EN,
  input  [7:0] RingCounter,
  output P0,
  output P1,
  output P2,
  output P3,
  output P4,
  output P5,
  output A0,
  output A1,
  output Cr,
  output Mr,
  output Mw,
  output Lalt,
  output incpc
);

  wire and_1_out, and_2_out, and_5_out, and_6_out, and_8_out, and_9_out;

  and and_1 (and_1_out, RingCounter[0], EN);
  and and_2 (and_2_out, RingCounter[1], EN);
  or or_1 (P1, and_1_out, P0, incpc);
  and and_3 (incpc, RingCounter[2], EN);
  and and_4 (P0, RingCounter[3], EN);
  or or_2 (P3, and_1_out, P0, and_5_out, and_2_out);
  and and_5 (and_5_out, RingCounter[4], EN);
  or or_3 (P4, and_2_out, incpc);
  and and_6 (and_6_out, RingCounter[5], EN);
  or or_4 (P5, and_2_out, and_6_out);
  // AND_Gate and_7 has open pins: in0=RingCounter[6], in1=EN, out=open
  and and_8 (and_8_out, RingCounter[7], EN);
  buf and_9 (and_9_out, EN);  // AND_Gate
  or or_5 (Cr, and_8_out, and_9_out);
  or or_6 (Mr, and_2_out, and_5_out, and_6_out);

  assign P2 = P0;

  // Notes on the sheet:
  //   In - register - Out
  //   3 -   MAR    - 0
  //   4 -     PC     - 1
  //   3,4 -  MBR  - 0,1
  //   5 -     AC     - 2
  //   5,3 - InReg - 2,0
  //   5,4 - OutReg - 2,1
  //   5,4,3 -  IR  - 2,1,0
endmodule

module StoreI (
  input  EN,
  input  [7:0] RingCounter,
  output P0,
  output P1,
  output P2,
  output P3,
  output P4,
  output P5,
  output A0,
  output A1,
  output Cr,
  output Mr,
  output Mw,
  output Lalt,
  output incpc
);

  wire and_1_out, and_5_out, and_8_out, and_9_out;

  and and_1 (and_1_out, RingCounter[0], EN);
  and and_2 (P5, RingCounter[1], EN);
  or or_1 (P1, and_1_out, P0, incpc);
  and and_3 (incpc, RingCounter[2], EN);
  or or_2 (P2, P0, Mw);
  and and_4 (P0, RingCounter[3], EN);
  or or_3 (P3, and_1_out, P0, and_5_out, P5);
  and and_5 (and_5_out, RingCounter[4], EN);
  or or_4 (P4, P5, incpc);
  and and_6 (Mw, RingCounter[5], EN);
  // AND_Gate and_7 has open pins: in0=RingCounter[6], in1=EN, out=open
  and and_8 (and_8_out, RingCounter[7], EN);
  buf and_9 (and_9_out, EN);  // AND_Gate
  or or_5 (Cr, and_8_out, and_9_out);
  or or_6 (Mr, P5, and_5_out);

  // Notes on the sheet:
  //   In - register - Out
  //   3 -   MAR    - 0
  //   4 -     PC     - 1
  //   3,4 -  MBR  - 0,1
  //   5 -     AC     - 2
  //   5,3 - InReg - 2,0
  //   5,4 - OutReg - 2,1
  //   5,4,3 -  IR  - 2,1,0
endmodule

module F (
  input  EN,
  input  [7:0] RingCounter,
  output P0,
  output P1,
  output P2,
  output P3,
  output P4,
  output P5,
  output A0,
  output A1,
  output Cr,
  output Mr,
  output Mw,
  output Lalt,
  output incpc
);

  wire and_1_out, and_5_out, and_6_out;

  and and_1 (and_1_out, RingCounter[0], EN);
  and and_2 (P5, RingCounter[1], EN);
  or or_1 (P1, and_1_out, P0, incpc);
  and and_3 (incpc, RingCounter[2], EN);
  and and_4 (P0, RingCounter[3], EN);
  or or_2 (P3, and_1_out, P0, and_5_out, P5);
  and and_5 (and_5_out, RingCounter[4], EN);
  or or_3 (P4, P5, incpc);
  and and_6 (and_6_out, RingCounter[5], EN);
  // AND_Gate and_7 has open pins: in0=RingCounter[6], in1=EN, out=open
  // AND_Gate and_8 has open pins: in0=RingCounter[7], in1=EN, out=open
  // AND_Gate and_9 has open pins: in1=EN, out=open
  or or_4 (Mr, P5, and_5_out, and_6_out);

  assign P2 = P0;

  // Notes on the sheet:
  //   In - register - Out
  //   3 -   MAR    - 0
  //   4 -     PC     - 1
  //   3,4 -  MBR  - 0,1
  //   5 -     AC     - 2
  //   5,3 - InReg - 2,0
  //   5,4 - OutReg - 2,1
  //   5,4,3 -  IR  - 2,1,0
endmodule

module skplogic (
  input  b11,
  input  b10,
  input  [15:0] AC,
  output skip
);

  wire and_1_out, and_2_out, and_3_out, comparator_1_eq, comparator_1_gt, comparator_1_lt;

  Comparator #(.width(16)) comparator_1 (
    .a(AC), .b({16{1'b0}}), .gt(comparator_1_gt), .eq(comparator_1_eq), .lt(comparator_1_lt));
  and and_1 (and_1_out, ~b11, ~b10, comparator_1_lt);  // AND_Gate
  and and_2 (and_2_out, ~b11, b10, comparator_1_eq);  // AND_Gate
  or Skipswitch (skip, and_1_out, and_2_out, and_3_out);
  and and_3 (and_3_out, b11, ~b10, comparator_1_gt);  // AND_Gate

  // Notes on the sheet:
  //   0,0
  //   0,1
  //   1,0
endmodule

module incpc (
  input  EN,
  input  [15:0] Busin,
  output [15:0] addout
);

  wire [15:0] adder_1_out;

  Adder #(.width(16)) adder_1 (.a(Busin), .b(16'h1), .out(adder_1_out));  // open: cin, cout
  assign addout = EN ? adder_1_out : 16'bz;  // Controlled_Buffer controlled_buffer_1
endmodule

module pcmerger (
  input  [15:0] BussIn,
  input  switch,
  input  [15:0] DataIn,
  output [15:0] outp
);

  wire not_1_out;

  not not_1 (not_1_out, switch);
  assign outp = not_1_out ? BussIn : 16'bz;  // Controlled_Buffer controlled_buffer_1
  assign outp = switch ? DataIn : 16'bz;  // Controlled_Buffer controlled_buffer_2
endmodule

module newadd (
  input  EN,
  input  [7:0] RingCounter,
  output P0,
  output P1,
  output P2,
  output P3,
  output P4,
  output P5,
  output A0,
  output A1,
  output Cr,
  output Mr,
  output Mw,
  output Lalt,
  output IncPC
);

  wire and_1_out, and_5_out, and_7_out, and_8_out, and_9_out;

  and and_1 (and_1_out, RingCounter[0], EN);
  and and_2 (P5, RingCounter[1], EN);
  or or_1 (P1, and_1_out, P0, IncPC);
  and and_3 (IncPC, RingCounter[2], EN);
  and and_4 (P0, RingCounter[3], EN);
  or or_2 (P3, and_1_out, P0, and_5_out, P5);
  and and_5 (and_5_out, RingCounter[4], EN);
  or or_3 (P4, P5, and_5_out, IncPC);
  // AND_Gate and_6 has open pins: in0=RingCounter[5], in1=EN, out=open
  and and_7 (and_7_out, RingCounter[6], EN);
  and and_8 (and_8_out, RingCounter[7], EN);
  buf and_9 (and_9_out, EN);  // AND_Gate
  or or_4 (Cr, and_7_out, and_8_out, and_9_out);
  or or_5 (Mr, P5, and_5_out);

  assign P2 = P0;

  // Notes on the sheet:
  //   In - register - Out
  //   3 -   MAR    - 0
  //   4 -     PC     - 1
  //   3,4 -  MBR  - 0,1
  //   5 -     AC     - 2
  //   5,3 - InReg - 2,0
  //   5,4 - OutReg - 2,1
  //   5,4,3 -  IR  - 2,1,0
endmodule

module JnS (
  input  EN,
  input  [7:0] RingCounter,
  output P0,
  output P1,
  output P2,
  output P3,
  output P4,
  output P5,
  output A0,
  output A1,
  output Cr,
  output Mr,
  output Mw,
  output Lalt,
  output IncPC
);

  wire and_1_out, and_3_out, and_6_out;

  and and_1 (and_1_out, RingCounter[0], EN);
  and and_2 (P5, RingCounter[1], EN);
  or or_1 (P1, and_1_out, P0, Mw, and_3_out);
  and and_3 (and_3_out, RingCounter[2], EN);
  and and_4 (P0, RingCounter[3], EN);
  or or_2 (P3, and_1_out, P0, P5);
  and and_5 (Mw, RingCounter[4], EN);
  or or_3 (P4, P5, and_6_out, and_3_out);
  and and_6 (and_6_out, RingCounter[5], EN);
  // AND_Gate and_7 has open pins: in0=RingCounter[6], in1=EN, out=open
  and and_8 (Cr, RingCounter[7], EN);
  or or_4 (Mr, P5, and_6_out);
  buf or_5 (IncPC, and_3_out);  // OR_Gate

  assign P2 = P0;

  // Notes on the sheet:
  //   In - register - Out
  //   3 -   MAR    - 0
  //   4 -     PC     - 1
  //   3,4 -  MBR  - 0,1
  //   5 -     AC     - 2
  //   5,3 - InReg - 2,0
  //   5,4 - OutReg - 2,1
  //   5,4,3 -  IR  - 2,1,0
endmodule

module FatOr (
  input  [12:0] TopInput,
  input  [12:0] SideInut,
  output [12:0] SideOut
);

  assign SideOut = TopInput | SideInut;  // OR_Gate or_1, 13 bits wide
endmodule

module BaseBus (
  input  EN,
  input  [7:0] RingCounter,
  output [12:0] BussOut
);

  wire and_1_out, and_5_out, and_6_out, and_7_out, and_8_out, and_9_out;

  and and_1 (and_1_out, RingCounter[0], EN);
  and and_2 (BussOut[9], RingCounter[1], EN);
  or or_1 (BussOut[1], and_1_out, BussOut[12]);
  and and_3 (BussOut[12], RingCounter[2], EN);
  // AND_Gate and_4 has open pins: in0=RingCounter[3], in1=EN, out=open
  or or_2 (BussOut[3], and_1_out, BussOut[9]);
  and and_5 (and_5_out, RingCounter[4], EN);
  or or_3 (BussOut[4], BussOut[9], BussOut[12]);
  and and_6 (and_6_out, RingCounter[5], EN);
  and and_7 (and_7_out, RingCounter[6], EN);
  and and_8 (and_8_out, RingCounter[7], EN);
  buf and_9 (and_9_out, EN);  // AND_Gate
  or or_4 (BussOut[8], and_5_out, and_6_out, and_7_out, and_8_out, and_9_out);

  assign BussOut[5] = BussOut[9];

  // Notes on the sheet:
  //   P0
  //   P1
  //   P2
  //   P3
  //   P4
  //   P5
  //   A0
  //   A1
  //   Cr
  //   Mr
  //   Mw
  //   Lalt
  //   IncPC
  //   In - register - Out
  //   3 -   MAR    - 0
  //   4 -     PC     - 1
  //   3,4 -  MBR  - 0,1
  //   5 -     AC     - 2
  //   5,3 - InReg - 2,0
  //   5,4 - OutReg - 2,1
  //   5,4,3 -  IR  - 2,1,0
endmodule

module ControlUnit2 (
  input  En,
  input  [7:0] RingCounter,
  input  [15:0] Instruction,
  output STOP,
  output P0,
  output P1,
  output P2,
  output P3,
  output P4,
  output P5,
  output A0,
  output A1,
  output Cr,
  output Mr,
  output Mw,
  output Lalt,
  output IncPC
);

  wire decoder_1_out0, decoder_1_out1, decoder_1_out2, decoder_1_out3, decoder_1_out4, decoder_1_out5,
       decoder_1_out6, decoder_1_out7, decoder_1_out8, decoder_1_out9, decoder_1_out10, decoder_1_out11,
       decoder_1_out12, decoder_1_out13, decoder_1_out14, decoder_1_out15;
  wire [12:0] addbuss_1_bussout, addlbuss_1_bussout, clearbuss_1_bussout, fator_2_sideout, fator_3_sideout,
       fator_4_sideout, fator_5_sideout, fator_6_sideout, fator_7_sideout, fator_8_sideout, fator_9_sideout,
       fator_10_sideout, fator_11_sideout, fator_12_sideout, fator_13_sideout, fator_14_sideout,
       fator_15_sideout, fator_16_sideout, haltbuss_1_bussout, jnsbuss_1_bussout, jumpbuss_1_bussout,
       jumplbuss_1_bussout, loadbuss_1_bussout, loadlbuss_1_bussout, outputbuss_1_bussout,
       skipbuss_1_bussout, storebuss_1_bussout, storeibuss_1_bussout, subtbuss_1_bussout, tslbuss_1_bussout,
       valinbuss_1_bussout;
  wire [15:0] undriven;

  Decoder #(.select(4)) decoder_1 (
    .out0(decoder_1_out0), .out1(decoder_1_out1), .out2(decoder_1_out2), .out3(decoder_1_out3),
    .out4(decoder_1_out4), .out5(decoder_1_out5), .out6(decoder_1_out6), .out7(decoder_1_out7),
    .out8(decoder_1_out8), .out9(decoder_1_out9), .out10(decoder_1_out10), .out11(decoder_1_out11),
    .out12(decoder_1_out12), .out13(decoder_1_out13), .out14(decoder_1_out14), .out15(decoder_1_out15),
    .sel(Instruction[15:12]), .en(En));
  JnSBuss jnsbuss_1 (.EN(decoder_1_out0), .RingCounter(RingCounter), .BussOut(jnsbuss_1_bussout));
  FatOr fator_1 (
    .TopInput(jnsbuss_1_bussout), .SideInut(fator_2_sideout),
    .SideOut({IncPC, Lalt, Mw, Mr, Cr, A1, A0, P5, P4, P3, P2, P1, P0}));
  Loadbuss loadbuss_1 (.EN(decoder_1_out1), .RingCounter(RingCounter), .BussOut(loadbuss_1_bussout));
  FatOr fator_2 (.TopInput(loadbuss_1_bussout), .SideInut(fator_3_sideout), .SideOut(fator_2_sideout));
  StoreBuss storebuss_1 (.EN(decoder_1_out2), .RingCounter(RingCounter), .BussOut(storebuss_1_bussout));
  FatOr fator_3 (.TopInput(storebuss_1_bussout), .SideInut(fator_4_sideout), .SideOut(fator_3_sideout));
  AddBuss addbuss_1 (.En(decoder_1_out3), .RingCounter(RingCounter), .BussOut(addbuss_1_bussout));
  FatOr fator_4 (.TopInput(addbuss_1_bussout), .SideInut(fator_5_sideout), .SideOut(fator_4_sideout));
  subtBuss subtbuss_1 (.En(decoder_1_out4), .RingCounter(RingCounter), .BussOut(subtbuss_1_bussout));
  FatOr fator_5 (.TopInput(subtbuss_1_bussout), .SideInut(fator_6_sideout), .SideOut(fator_5_sideout));
  ValInBuss valinbuss_1 (.EN(decoder_1_out5), .RingCounter(RingCounter), .BussOut(valinbuss_1_bussout));
  FatOr fator_6 (.TopInput(valinbuss_1_bussout), .SideInut(fator_7_sideout), .SideOut(fator_6_sideout));
  OutputBuss outputbuss_1 (.EN(decoder_1_out6), .RingCounter(RingCounter), .BussOut(outputbuss_1_bussout));
  FatOr fator_7 (.TopInput(outputbuss_1_bussout), .SideInut(fator_8_sideout), .SideOut(fator_7_sideout));
  HaltBuss haltbuss_1 (.EN(decoder_1_out7), .RingCounter(RingCounter), .BussOut(haltbuss_1_bussout));  // open: STOP
  FatOr fator_8 (.TopInput(haltbuss_1_bussout), .SideInut(fator_9_sideout), .SideOut(fator_8_sideout));
  SkipBuss skipbuss_1 (
    .EN(decoder_1_out8), .RingCounter(RingCounter), .AC(undriven), .data(Instruction[11:0]),
    .BussOut(skipbuss_1_bussout));
  FatOr fator_9 (.TopInput(skipbuss_1_bussout), .SideInut(fator_10_sideout), .SideOut(fator_9_sideout));
  JumpBuss jumpbuss_1 (.EN(decoder_1_out9), .RingCounter(RingCounter), .BussOut(jumpbuss_1_bussout));
  FatOr fator_10 (.TopInput(jumpbuss_1_bussout), .SideInut(fator_11_sideout), .SideOut(fator_10_sideout));
  ClearBuss clearbuss_1 (.EN(decoder_1_out10), .RingCounter(RingCounter), .BussOut(clearbuss_1_bussout));
  FatOr fator_11 (.TopInput(clearbuss_1_bussout), .SideInut(fator_12_sideout), .SideOut(fator_11_sideout));
  AddLBuss addlbuss_1 (.EN(decoder_1_out11), .RingCounter(RingCounter), .BussOut(addlbuss_1_bussout));
  FatOr fator_12 (.TopInput(addlbuss_1_bussout), .SideInut(fator_13_sideout), .SideOut(fator_12_sideout));
  JumpLBuss jumplbuss_1 (.EN(decoder_1_out12), .RingCounter(RingCounter), .BussOut(jumplbuss_1_bussout));
  FatOr fator_13 (.TopInput(jumplbuss_1_bussout), .SideInut(fator_14_sideout), .SideOut(fator_13_sideout));
  LoadLBuss loadlbuss_1 (.EN(decoder_1_out13), .RingCounter(RingCounter), .BussOut(loadlbuss_1_bussout));
  FatOr fator_14 (.TopInput(loadlbuss_1_bussout), .SideInut(fator_15_sideout), .SideOut(fator_14_sideout));
  StoreIBuss storeibuss_1 (.EN(decoder_1_out14), .RingCounter(RingCounter), .BussOut(storeibuss_1_bussout));
  FatOr fator_15 (.TopInput(storeibuss_1_bussout), .SideInut(fator_16_sideout), .SideOut(fator_15_sideout));
  TSLBuss tslbuss_1 (.EN(decoder_1_out15), .RingCounter(RingCounter), .BussOut(tslbuss_1_bussout));
  FatOr fator_16 (.TopInput(tslbuss_1_bussout), .SideInut({13{1'b0}}), .SideOut(fator_16_sideout));

  // Notes on the sheet:
  //   Instruction: initial=0x3021
endmodule

module JnSBuss (
  input  EN,
  input  [7:0] RingCounter,
  output [12:0] BussOut
);

  wire and_1_out, and_6_out;

  and and_1 (and_1_out, RingCounter[0], EN);
  and and_2 (BussOut[5], RingCounter[1], EN);
  or or_1 (BussOut[1], and_1_out, BussOut[2], BussOut[10], BussOut[12]);
  and and_3 (BussOut[12], RingCounter[2], EN);
  and and_4 (BussOut[2], RingCounter[3], EN);
  or or_2 (BussOut[3], and_1_out, BussOut[2], BussOut[5]);
  and and_5 (BussOut[10], RingCounter[4], EN);
  or or_3 (BussOut[4], BussOut[5], and_6_out, BussOut[12]);
  and and_6 (and_6_out, RingCounter[5], EN);
  // AND_Gate and_7 has open pins: in0=RingCounter[6], in1=EN, out=open
  and and_8 (BussOut[8], RingCounter[7], EN);
  or or_4 (BussOut[9], BussOut[5], and_6_out);

  assign BussOut[0] = BussOut[2];

  // Notes on the sheet:
  //   P0
  //   P1
  //   P2
  //   P3
  //   P4
  //   P5
  //   A0
  //   A1
  //   Cr
  //   Mr
  //   Mw
  //   Lalt
  //   IncPC
  //   In - register - Out
  //   3 -   MAR    - 0
  //   4 -     PC     - 1
  //   3,4 -  MBR  - 0,1
  //   5 -     AC     - 2
  //   5,3 - InReg - 2,0
  //   5,4 - OutReg - 2,1
  //   5,4,3 -  IR  - 2,1,0
endmodule

module Loadbuss (
  input  EN,
  input  [7:0] RingCounter,
  output [12:0] BussOut
);

  wire and_1_out, and_2_out, and_5_out, and_7_out, and_8_out;

  and and_1 (and_1_out, RingCounter[0], EN);
  and and_2 (and_2_out, RingCounter[1], EN);
  or or_1 (BussOut[1], and_1_out, BussOut[2], BussOut[12]);
  and and_3 (BussOut[12], RingCounter[2], EN);
  and and_4 (BussOut[2], RingCounter[3], EN);
  or or_2 (BussOut[3], and_1_out, BussOut[2], and_2_out);
  and and_5 (and_5_out, RingCounter[4], EN);
  or or_3 (BussOut[4], and_2_out, BussOut[12]);
  // AND_Gate and_6 has open pins: in0=RingCounter[5], in1=EN, out=open
  or or_4 (BussOut[5], and_2_out, and_5_out);
  and and_7 (and_7_out, RingCounter[6], EN);
  and and_8 (and_8_out, RingCounter[7], EN);
  or or_5 (BussOut[8], and_7_out, and_8_out);
  or or_6 (BussOut[9], and_2_out, and_5_out);

  assign {BussOut[11:10], BussOut[7:6], BussOut[0]} = {4'b0000, BussOut[2]};

  // Notes on the sheet:
  //   P0
  //   P1
  //   P2
  //   P3
  //   P4
  //   P5
  //   A0
  //   A1
  //   Cr
  //   Mr
  //   Mw
  //   Lalt
  //   IncPC
endmodule

module StoreBuss (
  input  EN,
  input  [7:0] RingCounter,
  output [12:0] BussOut
);

  wire and_1_out, and_7_out, and_8_out;

  and and_1 (and_1_out, RingCounter[0], EN);
  and and_2 (BussOut[9], RingCounter[1], EN);
  or or_1 (BussOut[1], and_1_out, BussOut[0], BussOut[12]);
  and and_3 (BussOut[12], RingCounter[2], EN);
  or or_2 (BussOut[2], BussOut[0], BussOut[10]);
  and and_4 (BussOut[0], RingCounter[3], EN);
  or or_3 (BussOut[3], and_1_out, BussOut[0], BussOut[9]);
  and and_5 (BussOut[10], RingCounter[4], EN);
  or or_4 (BussOut[4], BussOut[9], BussOut[12]);
  // AND_Gate and_6 has open pins: in0=RingCounter[5], in1=EN, out=open
  and and_7 (and_7_out, RingCounter[6], EN);
  and and_8 (and_8_out, RingCounter[7], EN);
  or or_5 (BussOut[8], and_7_out, and_8_out);

  assign BussOut[5] = BussOut[9];

  // Notes on the sheet:
  //   In - register - Out
  //   3 -   MAR    - 0
  //   4 -     PC     - 1
  //   3,4 -  MBR  - 0,1
  //   5 -     AC     - 2
  //   5,3 - InReg - 2,0
  //   5,4 - OutReg - 2,1
  //   5,4,3 -  IR  - 2,1,0
  //   P0
  //   P1
  //   P2
  //   P3
  //   P4
  //   P5
  //   A0
  //   A1
  //   Cr
  //   Mr
  //   Mw
  //   Lalt
  //   IncPC
endmodule

module AddBuss (
  input  En,
  input  [7:0] RingCounter,
  output [12:0] BussOut
);

  wire and_2_out, and_5_out, and_6_out;

  and and_1 (BussOut[2], RingCounter[3], En);
  or or_1 (BussOut[1], BussOut[2], BussOut[12], and_5_out);
  and and_2 (and_2_out, RingCounter[4], En);
  and and_3 (BussOut[11], En, RingCounter[5]);
  or out3 (BussOut[3], BussOut[2], and_5_out, and_6_out, and_2_out);
  and and_4 (BussOut[8], RingCounter[7], En);
  or or_2 (BussOut[4], and_6_out, BussOut[12], and_2_out);
  or or_3 (BussOut[5], and_6_out, BussOut[11]);
  and and_5 (and_5_out, RingCounter[0], En);
  and and_6 (and_6_out, RingCounter[1], En);
  or or_4 (BussOut[9], and_2_out, and_6_out);
  and and_7 (BussOut[12], RingCounter[2], En);

  assign {BussOut[10], BussOut[7], BussOut[0]} = {2'b00, BussOut[2]};

  // Notes on the sheet:
  //   In - register - Out
  //   3 -   MAR    - 0
  //   4 -     PC     - 1
  //   3,4 -  MBR  - 0,1
  //   5 -     AC     - 2
  //   5,3 - InReg - 2,0
  //   5,4 - OutReg - 2,1
  //   5,4,3 -  IR  - 2,1,0
  //   P0
  //   ADD=0011
  //   P1
  //   P2
  //   P3
  //   P4
  //   P5
  //   A0
  //   A1
  //   Cr
  //   Mr
  //   Mw
  //   Lalt
  //   IncPC
endmodule

module subtBuss (
  input  En,
  input  [7:0] RingCounter,
  output [12:0] BussOut
);

  wire and_2_out, and_5_out, and_6_out;

  and and_1 (BussOut[2], RingCounter[3], En);
  or or_1 (BussOut[1], BussOut[2], BussOut[12], and_5_out);
  and and_2 (and_2_out, RingCounter[4], En);
  and and_3 (BussOut[11], En, RingCounter[5]);
  or out3 (BussOut[3], BussOut[2], and_5_out, and_6_out, and_2_out);
  and and_4 (BussOut[8], RingCounter[7], En);
  or or_2 (BussOut[4], and_6_out, BussOut[12], and_2_out);
  or or_3 (BussOut[5], and_6_out, BussOut[11]);
  and and_5 (and_5_out, RingCounter[0], En);
  and and_6 (and_6_out, RingCounter[1], En);
  or or_4 (BussOut[9], and_2_out, and_6_out);
  and and_7 (BussOut[12], RingCounter[2], En);

  assign {BussOut[10], BussOut[7:6], BussOut[0]} = {1'b0, BussOut[11], 1'b0, BussOut[2]};

  // Notes on the sheet:
  //   P0
  //   ADD=0011
  //   P1
  //   P2
  //   P3
  //   P4
  //   P5
  //   A0
  //   A1
  //   Cr
  //   Mr
  //   Mw
  //   Lalt
  //   IncPC
endmodule

module ValInBuss (
  input  EN,
  input  [7:0] RingCounter,
  output [12:0] BussOut
);

  wire and_1_out, and_6_out, and_7_out, and_8_out;

  and and_1 (and_1_out, RingCounter[0], EN);
  and and_2 (BussOut[9], RingCounter[1], EN);
  or or_1 (BussOut[1], and_1_out, BussOut[12]);
  and and_3 (BussOut[12], RingCounter[2], EN);
  and and_4 (BussOut[2], RingCounter[3], EN);
  or or_2 (BussOut[3], and_1_out, BussOut[9]);
  // AND_Gate and_5 has open pins: in0=RingCounter[4], in1=EN, out=open
  or or_3 (BussOut[4], BussOut[9], BussOut[12]);
  and and_6 (and_6_out, RingCounter[5], EN);
  or or_4 (BussOut[5], BussOut[9], BussOut[2]);
  and and_7 (and_7_out, RingCounter[6], EN);
  and and_8 (and_8_out, RingCounter[7], EN);
  or or_5 (BussOut[8], and_6_out, and_7_out, and_8_out);

  assign BussOut[0] = BussOut[2];

  // Notes on the sheet:
  //   P0
  //   P1
  //   P2
  //   P3
  //   P4
  //   P5
  //   A0
  //   A1
  //   Cr
  //   Mr
  //   Mw
  //   Lalt
  //   IncPC
  //   In - register - Out
  //   3 -   MAR    - 0
  //   4 -     PC     - 1
  //   3,4 -  MBR  - 0,1
  //   5 -     AC     - 2
  //   5,3 - InReg - 2,0
  //   5,4 - OutReg - 2,1
  //   5,4,3 -  IR  - 2,1,0
endmodule

module OutputBuss (
  input  EN,
  input  [7:0] RingCounter,
  output [12:0] BussOut
);

  wire and_1_out, and_6_out, and_7_out, and_8_out;

  and and_1 (and_1_out, RingCounter[0], EN);
  and and_2 (BussOut[9], RingCounter[1], EN);
  or or_1 (BussOut[1], and_1_out, BussOut[12]);
  and and_3 (BussOut[12], RingCounter[2], EN);
  and and_4 (BussOut[2], RingCounter[3], EN);
  or or_2 (BussOut[3], and_1_out, BussOut[9]);
  // AND_Gate and_5 has open pins: in0=RingCounter[4], in1=EN, out=open
  or or_3 (BussOut[4], BussOut[9], BussOut[2], BussOut[12]);
  and and_6 (and_6_out, RingCounter[5], EN);
  or or_4 (BussOut[5], BussOut[9], BussOut[2]);
  and and_7 (and_7_out, RingCounter[6], EN);
  and and_8 (and_8_out, RingCounter[7], EN);
  or or_5 (BussOut[8], and_6_out, and_7_out, and_8_out);

  // Notes on the sheet:
  //   P0
  //   P1
  //   P2
  //   P3
  //   P4
  //   P5
  //   A0
  //   A1
  //   Cr
  //   Mr
  //   Mw
  //   Lalt
  //   IncPC
endmodule

module HaltBuss (
  input  EN,
  input  [7:0] RingCounter,
  output STOP,
  output [12:0] BussOut
);


  assign BussOut = {13{1'b0}};
  assign STOP = EN;

  // Notes on the sheet:
  //   In - register - Out
  //   3 -   MAR    - 0
  //   4 -     PC     - 1
  //   3,4 -  MBR  - 0,1
  //   5 -     AC     - 2
  //   5,3 - InReg - 2,0
  //   5,4 - OutReg - 2,1
  //   5,4,3 -  IR  - 2,1,0
endmodule

module SkipBuss (
  input  EN,
  input  [7:0] RingCounter,
  input  [15:0] AC,
  input  [11:0] data,
  output [12:0] BussOut
);

  wire and_1_out, and_3_out, and_4_out, and_6_out, and_7_out, and_8_out, skplogic_1_skip;

  skplogic skplogic_1 (.b11(data[11]), .b10(data[10]), .AC(AC), .skip(skplogic_1_skip));
  and and_1 (and_1_out, RingCounter[0], EN);
  and and_2 (BussOut[9], RingCounter[1], EN);
  or or_1 (BussOut[1], and_1_out, and_4_out, and_3_out);
  and and_3 (and_3_out, RingCounter[2], EN);
  and and_4 (and_4_out, RingCounter[3], skplogic_1_skip, EN);
  or or_2 (BussOut[3], and_1_out, BussOut[9]);
  // AND_Gate and_5 has open pins: in0=RingCounter[4], in1=EN, out=open
  or or_3 (BussOut[4], BussOut[9], and_4_out, and_3_out);
  and and_6 (and_6_out, RingCounter[5], EN);
  and and_7 (and_7_out, RingCounter[6], EN);
  and and_8 (and_8_out, RingCounter[7], EN);
  or or_4 (BussOut[8], and_6_out, and_7_out, and_8_out);
  or or_5 (BussOut[12], and_3_out, and_4_out);

  assign BussOut[5] = BussOut[9];

  // Notes on the sheet:
  //   P0
  //   P1
  //   P2
  //   P3
  //   P4
  //   P5
  //   A0
  //   A1
  //   Cr
  //   Mr
  //   Mw
  //   In - register - Out
  //   3 -   MAR    - 0
  //   4 -     PC     - 1
  //   3,4 -  MBR  - 0,1
  //   5 -     AC     - 2
  //   5,3 - InReg - 2,0
  //   5,4 - OutReg - 2,1
  //   5,4,3 -  IR  - 2,1,0
  //   Lalt
  //   IncPC
endmodule

module JumpBuss (
  input  EN,
  input  [7:0] RingCounter,
  output [12:0] BussOut
);

  wire and_1_out, and_6_out, and_7_out, and_8_out;

  and and_1 (and_1_out, RingCounter[0], EN);
  and and_2 (BussOut[9], RingCounter[1], EN);
  or or_1 (BussOut[1], and_1_out, BussOut[2], BussOut[12]);
  and and_3 (BussOut[12], RingCounter[2], EN);
  and and_4 (BussOut[2], RingCounter[3], EN);
  or or_2 (BussOut[3], and_1_out, BussOut[9]);
  // AND_Gate and_5 has open pins: in0=RingCounter[4], in1=EN, out=open
  or or_3 (BussOut[4], BussOut[9], BussOut[2], BussOut[12]);
  and and_6 (and_6_out, RingCounter[5], EN);
  and and_7 (and_7_out, RingCounter[6], EN);
  and and_8 (and_8_out, RingCounter[7], EN);
  or or_4 (BussOut[8], and_6_out, and_7_out, and_8_out);

  assign {BussOut[5], BussOut[0]} = {BussOut[9], BussOut[2]};

  // Notes on the sheet:
  //   P0
  //   P1
  //   P2
  //   P3
  //   P4
  //   P5
  //   A0
  //   A1
  //   Cr
  //   Mr
  //   Mw
  //   Lalt
  //   IncPC
endmodule

module ClearBuss (
  input  EN,
  input  [7:0] RingCounter,
  output [12:0] BussOut
);

  wire and_1_out, and_7_out, and_8_out;

  and and_1 (and_1_out, RingCounter[0], EN);
  and and_2 (BussOut[9], RingCounter[1], EN);
  or or_1 (BussOut[1], and_1_out, BussOut[12]);
  and and_3 (BussOut[12], RingCounter[2], EN);
  and and_4 (BussOut[2], RingCounter[3], EN);
  or or_2 (BussOut[3], and_1_out, BussOut[2], BussOut[9]);
  and and_5 (BussOut[11], RingCounter[4], EN);
  or or_3 (BussOut[4], BussOut[9], BussOut[2], BussOut[12]);
  // AND_Gate and_6 has open pins: in0=RingCounter[5], in1=EN, out=open
  or or_4 (BussOut[5], BussOut[9], BussOut[11]);
  and and_7 (and_7_out, RingCounter[6], EN);
  and and_8 (and_8_out, RingCounter[7], EN);
  or or_5 (BussOut[8], and_7_out, and_8_out);

  assign BussOut[7] = BussOut[11];

  // Notes on the sheet:
  //   P0
  //   P1
  //   P2
  //   P3
  //   P4
  //   P5
  //   A0
  //   A1
  //   Cr
  //   Mr
  //   Mw
  //   Lalt
  //   IncPC
  //   In - register - Out
  //   3 -   MAR    - 0
  //   4 -     PC     - 1
  //   3,4 -  MBR  - 0,1
  //   5 -     AC     - 2
  //   5,3 - InReg - 2,0
  //   5,4 - OutReg - 2,1
  //   5,4,3 -  IR  - 2,1,0
endmodule

module AddLBuss (
  input  EN,
  input  [7:0] RingCounter,
  output [12:0] BussOut
);

  wire and_1_out, and_2_out, and_5_out, and_6_out;

  and and_1 (and_1_out, RingCounter[0], EN);
  and and_2 (and_2_out, RingCounter[1], EN);
  or or_1 (BussOut[1], and_1_out, BussOut[2], BussOut[12]);
  and and_3 (BussOut[12], RingCounter[2], EN);
  and and_4 (BussOut[2], RingCounter[3], EN);
  or or_2 (BussOut[3], and_1_out, BussOut[2], and_5_out, and_6_out, and_2_out);
  and and_5 (and_5_out, RingCounter[4], EN);
  or or_3 (BussOut[4], and_2_out, and_6_out, BussOut[12]);
  and and_6 (and_6_out, RingCounter[5], EN);
  or or_4 (BussOut[5], and_2_out, BussOut[11]);
  and and_7 (BussOut[11], RingCounter[6], EN);
  // AND_Gate and_8 has open pins: in0=RingCounter[7], in1=EN, out=open
  buf and_9 (BussOut[8], EN);  // AND_Gate
  or or_5 (BussOut[9], and_2_out, and_6_out, and_5_out);

  assign {BussOut[6], BussOut[0]} = {BussOut[11], BussOut[2]};

  // Notes on the sheet:
  //   P0
  //   P1
  //   P2
  //   P3
  //   P4
  //   P5
  //   A0
  //   A1
  //   Cr
  //   Mr
  //   Mw
  //   Lalt
  //   IncPC
  //   In - register - Out
  //   3 -   MAR    - 0
  //   4 -     PC     - 1
  //   3,4 -  MBR  - 0,1
  //   5 -     AC     - 2
  //   5,3 - InReg - 2,0
  //   5,4 - OutReg - 2,1
  //   5,4,3 -  IR  - 2,1,0
endmodule

module JumpLBuss (
  input  EN,
  input  [7:0] RingCounter,
  output [12:0] BussOut
);

  wire and_1_out, and_5_out, and_6_out, and_8_out, and_9_out;

  and and_1 (and_1_out, RingCounter[0], EN);
  and and_2 (BussOut[5], RingCounter[1], EN);
  or or_1 (BussOut[1], and_1_out, BussOut[2], BussOut[12]);
  and and_3 (BussOut[12], RingCounter[2], EN);
  and and_4 (BussOut[2], RingCounter[3], EN);
  or or_2 (BussOut[3], and_1_out, BussOut[2], and_5_out, BussOut[5]);
  and and_5 (and_5_out, RingCounter[4], EN);
  or or_3 (BussOut[4], BussOut[5], and_6_out, BussOut[12]);
  and and_6 (and_6_out, RingCounter[5], EN);
  // AND_Gate and_7 has open pins: in0=RingCounter[6], in1=EN, out=open
  and and_8 (and_8_out, RingCounter[7], EN);
  buf and_9 (and_9_out, EN);  // AND_Gate
  or or_4 (BussOut[8], and_8_out, and_9_out);
  or or_5 (BussOut[9], BussOut[5], and_5_out, and_6_out);

  assign BussOut[0] = BussOut[2];

  // Notes on the sheet:
  //   P0
  //   P1
  //   P2
  //   P3
  //   P4
  //   P5
  //   A0
  //   A1
  //   Cr
  //   Mr
  //   Mw
  //   Lalt
  //   IncPC
  //   In - register - Out
  //   3 -   MAR    - 0
  //   4 -     PC     - 1
  //   3,4 -  MBR  - 0,1
  //   5 -     AC     - 2
  //   5,3 - InReg - 2,0
  //   5,4 - OutReg - 2,1
  //   5,4,3 -  IR  - 2,1,0
endmodule

module LoadLBuss (
  input  EN,
  input  [7:0] RingCounter,
  output [12:0] BussOut
);

  wire and_1_out, and_2_out, and_5_out, and_6_out, and_8_out, and_9_out;

  and and_1 (and_1_out, RingCounter[0], EN);
  and and_2 (and_2_out, RingCounter[1], EN);
  or or_1 (BussOut[1], and_1_out, BussOut[2], BussOut[12]);
  and and_3 (BussOut[12], RingCounter[2], EN);
  and and_4 (BussOut[2], RingCounter[3], EN);
  or or_2 (BussOut[3], and_1_out, BussOut[2], and_5_out, and_2_out);
  and and_5 (and_5_out, RingCounter[4], EN);
  or or_3 (BussOut[4], and_2_out, BussOut[12]);
  and and_6 (and_6_out, RingCounter[5], EN);
  or or_4 (BussOut[5], and_2_out, and_6_out);
  // AND_Gate and_7 has open pins: in0=RingCounter[6], in1=EN, out=open
  and and_8 (and_8_out, RingCounter[7], EN);
  buf and_9 (and_9_out, EN);  // AND_Gate
  or or_5 (BussOut[8], and_8_out, and_9_out);
  or or_6 (BussOut[9], and_2_out, and_5_out, and_6_out);

  assign BussOut[0] = BussOut[2];

  // Notes on the sheet:
  //   P0
  //   P1
  //   P2
  //   P3
  //   P4
  //   P5
  //   A0
  //   A1
  //   Cr
  //   Mr
  //   Mw
  //   Lalt
  //   IncPC
  //   In - register - Out
  //   3 -   MAR    - 0
  //   4 -     PC     - 1
  //   3,4 -  MBR  - 0,1
  //   5 -     AC     - 2
  //   5,3 - InReg - 2,0
  //   5,4 - OutReg - 2,1
  //   5,4,3 -  IR  - 2,1,0
endmodule

module StoreIBuss (
  input  EN,
  input  [7:0] RingCounter,
  output [12:0] BussOut
);

  wire and_1_out, and_5_out, and_8_out, and_9_out;

  and and_1 (and_1_out, RingCounter[0], EN);
  and and_2 (BussOut[5], RingCounter[1], EN);
  or or_1 (BussOut[1], and_1_out, BussOut[0], BussOut[12]);
  and and_3 (BussOut[12], RingCounter[2], EN);
  or or_2 (BussOut[2], BussOut[0], BussOut[10]);
  and and_4 (BussOut[0], RingCounter[3], EN);
  or or_3 (BussOut[3], and_1_out, BussOut[0], and_5_out, BussOut[5]);
  and and_5 (and_5_out, RingCounter[4], EN);
  or or_4 (BussOut[4], BussOut[5], BussOut[12]);
  and and_6 (BussOut[10], RingCounter[5], EN);
  // AND_Gate and_7 has open pins: in0=RingCounter[6], in1=EN, out=open
  and and_8 (and_8_out, RingCounter[7], EN);
  buf and_9 (and_9_out, EN);  // AND_Gate
  or or_5 (BussOut[8], and_8_out, and_9_out);
  or or_6 (BussOut[9], BussOut[5], and_5_out);

  // Notes on the sheet:
  //   P0
  //   P1
  //   P2
  //   P3
  //   P4
  //   P5
  //   A0
  //   A1
  //   Cr
  //   Mr
  //   Mw
  //   Lalt
  //   IncPC
  //   In - register - Out
  //   3 -   MAR    - 0
  //   4 -     PC     - 1
  //   3,4 -  MBR  - 0,1
  //   5 -     AC     - 2
  //   5,3 - InReg - 2,0
  //   5,4 - OutReg - 2,1
  //   5,4,3 -  IR  - 2,1,0
endmodule

module TSLBuss (
  input  EN,
  input  [7:0] RingCounter,
  output [12:0] BussOut
);

  wire or_1_out;

  or or_1 (or_1_out, RingCounter[0], RingCounter[1], RingCounter[2], RingCounter[3], RingCounter[4], RingCounter[5], RingCounter[6], RingCounter[7]);
  and and_1 (BussOut[5], or_1_out, EN);

  assign {BussOut[11:6], BussOut[4:0]} = {{6{1'b0}}, {5{BussOut[5]}}};
endmodule
